# Fritzing sketch YMF825pico (saved by Fritzing 0.9.6b)
breadboards: 1

parts:
  Pico_H1 = Raspberry Pi Pico H [part_number="PICO/PICO W"]
  RE1 = Rotary Encoder [part_number="Rotary Encoder 1" package=THT]
  RE2 = Rotary Encoder [part_number="Rotary Encoder 2" package=THT]
  RE3 = Rotary Encoder [part_number="Rotary Encoder 3" package=THT]
  RE4 = Rotary Encoder [part_number="Rotary Encoder 4" package=THT]
  LED1 = smd LED [color="Red (633nm)" package="0603 [SMD]"]
  R1 = Resistor [tolerance=±5% resistance=330 package="0805 [SMD]"]
  Q2 = NPN-Transistor [part_number=2SC1815 package="TO92 [THT]"]
  R2 = Resistor [tolerance=±5% resistance=10k package="0805 [SMD]"]
  R3 = Resistor [tolerance=±5% resistance=220 package="0805 [SMD]"]
  OLED_I2C1 = OLED 128x64 I2C Monochrome Display [part_number=SSD1306]
  U1 = MIDI_CONN_FEMALE_SUPPORT [package=din_5_female_support]
  U2 = Sharp PC817 [part_number=FOD817 package=THT]
  Q1 = NPN-Transistor [part_number=2SC1815 package="TO92 [THT]"]
  D1 = Rectifier Diode 10A [part_number=1SS178]
  FM_Synthesizer = YMF825 breakout board [part_number=YMF825]

nets:
  N1: Pico_H1.VBUS, FM_Synthesizer.5V
  GND: Pico_H1.GND, RE1.EncoderPinC, RE2.EncoderPinC, RE3.EncoderPinC, RE4.EncoderPinC, LED1.cathode, Q2.E, OLED_I2C1.GND, Q1.E, FM_Synthesizer.GND
  N2: Pico_H1.3V3_EN, R2.Pin_1, OLED_I2C1.VDD, U2.Pin_4
  N3: Pico_H1.GP28_A2, R1.Pin_0
  N4: Pico_H1.GP22, FM_Synthesizer.RST_N
  N5: Pico_H1.GP21, OLED_I2C1.SCK
  N6: Pico_H1.GP20, OLED_I2C1.SDA
  N7: Pico_H1.GP19, FM_Synthesizer.MOSI
  N8: Pico_H1.GP18, FM_Synthesizer.SCK
  N9: Pico_H1.GP17, FM_Synthesizer.SS
  N10: Pico_H1.GP16, FM_Synthesizer.MISO
  N11: Pico_H1.GP9, RE4.EncoderPinB
  N12: Pico_H1.GP8, RE4.EncoderPinA
  N13: Pico_H1.GP7, RE3.EncoderPinB
  N14: Pico_H1.GP6, RE3.EncoderPinA
  N15: Pico_H1.GP5, RE2.EncoderPinB
  N16: Pico_H1.GP4, RE2.EncoderPinA
  N17: Pico_H1.GP3, RE1.EncoderPinB
  N18: Pico_H1.GP2, RE1.EncoderPinA
  N19: Pico_H1.GP1, R2.Pin_0, Q1.C
  N20: LED1.anode, R1.Pin_1
  N21: Q2.B, Q2.C, U2.Pin_3, Q1.B
  N22: R3.Pin_0, U1.MIDI_OUT
  N23: R3.Pin_1, U2.Pin_1, D1.cathode
  N24: U1.MIDI_IN, U2.Pin_2, D1.anode

custom parts:
  Raspberry Pi Pico H: Raspberry Pi Pico H. Based around the RP2040 microcontroller the Pico H is a low cost microcontroller device bringing Raspberry Pi quality, cost, and easy of use to the microcontroller space.
  YMF825 breakout board: YMF825 breakout board with audio power amp.

// code stored in the sketch: ymf825pico.py.ino
# -*- coding: utf-8 -*-
##################################################################################
# YMF825 synthesizer with Raspberry Pi PICO Class.
#
# Hardware Information:
#   YMF825 bottom view
#     1 2 3 4 5 6 7 8 9
#    -+-+-+-+-+-+-+-+-+-
#   | S M M C G V R     |
#   | S O I L N C S     |
#   |   S S K D C T     |
#   |   I O             |
#   |             Audio Jack
#    ---------------+---
#                   |
#                    ---Amp
#
#   PICO GPIO(pin)      YMF825 name(pin)    LED(n/a)
#     5V          (40)    VCC        (6)
#     GND         (38)    GND        (5)
#     SPI1 MOSI 19(25)    SPI MOSI   (2)
#     SPI1 MISO 16(21)    SPI MISO   (3)
#     SPI1 CLK  18( 24)    SPI CLK    (4)
#     SPI1 CS   17(22)    SS         (1)
#     RESET     22(29)    RESET      (7)
#n/a  LED       28(34)                      Anode---1K--->|---Cathode---GND
#
# Synthesizer Structure
#             ---PORTION0:VOICEa..b---TONEp---
#            |                                |
#            |---PORTION1:VOICEc..d---TONEq---|
#   TIMBREx--|                                |---SOUND--->YMF825
#            |---PORTION2:VOICEe..f---TONEr---|
#            |                                |
#             ---PORTION3:VOICEg..h---TONEs---
#
#     This synthesizer has TIMBRES timbres.
#     Each timbre has 4 portions.
#     Each portion is able to have some voices (from 0 to 16).
#     A voice is one of voice chanel in YMF825.  YMF825 has voices from 0 to 15. 
#     Each voice use a tone data.  Tone is a set of YMF825 sound parameters.
#
# Copyright (c) by Shunsuke Ohira
#   00.600 2022/05/09: For Pi400 (original)
#   00.100 2023/08/05: For PICO W
##################################################################################

from machine import Pin, SPI
import time
import json
import re
#from decimal import Decimal
import math


## YMF825 hardware control class for Raspberry Pi PICO W ##
class ymf825pico_class:

    # Initializer
    def __init__( self, file_tone_name = "YMF825ToneName.txt", file_tone_param = "YMF825ToneParm.txt", file_timbre_name = "YMF825TimbreName.txt", file_timbre_param = "YMF825TimbreParm.txt", file_equalizer_name = "YMF825EQName.txt", file_equalizer_param = "YMF825EQParm.txt", file_encode = "utf-8" ):
        # PICO GPIO and pin no.
        self.SPI_CH = 0
        self.SPIPORT_MOSI = 19    # pin25
        self.SPIPORT_MISO = 16    # pin21
        self.SPIPORT_CLK  = 18    # pin24
        self.SPIPORT_CE   = 17    # pin22
        self.YMF825_RESET = 22    # pin29
        self.GPIO_LED     = 28    # pin34    # N/A

        # SPI mode0
        self.SPI_MAX_SPEED_HZ = 1000000
        self.spi_cs = Pin(self.SPIPORT_CE, Pin.OUT)
        self.spi = SPI(self.SPI_CH, sck=Pin(self.SPIPORT_CLK), mosi=Pin(self.SPIPORT_MOSI), miso=Pin(self.SPIPORT_MISO), baudrate=self.SPI_MAX_SPEED_HZ, firstbit=SPI.MSB, polarity=0, phase=0)

        # YMF825 RESET pin
        self.YMF825_reset = Pin(self.YMF825_RESET, Pin.OUT)

        # LED (CURRENTLY NOT AVAILABLE)
        self.led_indicator = Pin(self.GPIO_LED, Pin.OUT)

        #Tone parameter [address(1byte)|data(35byte)].
        self.sound_param = bytearray(36)

        # Note number and Note name
        self.note_name = [
            "C_","C_#","D_","D_#","E_","F_","F_#","G_","G_#","A_","A_#","B_",
            "C0","C0#","D0","D0#","E0","F0","F0#","G0","G0#","A0","A0#","B0",
            "C1","C1#","D1","D1#","E1","F1","F1#","G1","G1#","A1","A1#","B1",
            "C2","C2#","D2","D2#","E2","F2","F2#","G2","G2#","A2","A2#","B2",
            "C3","C3#","D3","D3#","E3","F3","F3#","G3","G3#","A3","A3#","B3",
            "C4","C4#","D4","D4#","E4","F4","F4#","G4","G4#","A4","A4#","B4",
            "C5","C5#","D5","D5#","E5","F5","F5#","G5","G5#","A5","A5#","B5",
            "C6","C6#","D6","D6#","E6","F6","F6#","G6","G6#","A6","A6#","B6",
            "C7","C7#","D7","D7#","E7","F7","F7#","G7","G7#","A7","A7#","B7",
            "C8","C8#","D8","D8#","E8","F8","F8#","G8","G8#","A8","A8#","B8",
            "C9","C9#","D9","D9#","E9","F9","F9#","G9","G9#","A9","A9#","B9"
        ]

        # Note name and Note number
        self.note_dict = {
            "C_":  0,"C_#":  1,"D_":  2,"D_#":  3,"E_":  4,"F_":  5,"F_#":  6,"G_":  7,"G_#":  8,"A_":  9,"A_#": 10,"B_": 11,
            "C0": 12,"C0#": 13,"D0": 14,"D0#": 15,"E0": 16,"F0": 17,"F0#": 18,"G0": 19,"G0#": 20,"A0": 21,"A0#": 22,"B0": 23,
            "C1": 24,"C1#": 25,"D1": 26,"D1#": 27,"E1": 28,"F1": 29,"F1#": 30,"G1": 31,"G1#": 32,"A1": 33,"A1#": 34,"B1": 35,
            "C2": 36,"C2#": 37,"D2": 38,"D2#": 39,"E2": 40,"F2": 41,"F2#": 42,"G2": 43,"G2#": 44,"A2": 45,"A2#": 46,"B2": 47,
            "C3": 48,"C3#": 49,"D3": 50,"D3#": 51,"E3": 52,"F3": 53,"F3#": 54,"G3": 55,"G3#": 56,"A3": 57,"A3#": 58,"B3": 59,
            "C4": 60,"C4#": 61,"D4": 62,"D4#": 63,"E4": 64,"F4": 65,"F4#": 66,"G4": 67,"G4#": 68,"A4": 69,"A4#": 70,"B4": 71,
            "C5": 72,"C5#": 73,"D5": 74,"D5#": 75,"E5": 76,"F5": 77,"F5#": 78,"G5": 79,"G5#": 80,"A5": 81,"A5#": 82,"B5": 83,
            "C6": 84,"C6#": 85,"D6": 86,"D6#": 87,"E6": 88,"F6": 89,"F6#": 90,"G6": 91,"G6#": 92,"A6": 93,"A6#": 94,"B6": 95,
            "C7": 96,"C7#": 97,"D7": 98,"D7#": 99,"E7":100,"F7":101,"F7#":102,"G7":103,"G7#":104,"A7":105,"A7#":106,"B7":107,
            "C8":108,"C8#":109,"D8":110,"D8#":111,"E8":112,"F8":113,"F8#":114,"G8":115,"G8#":116,"A8":117,"A8#":118,"B8":119,
            "C9":128,"C9#":121,"D9":122,"D9#":123,"E9":124,"F9":125,"F9#":126,"G9":127,"G9#":128,"A9":129,"A9#":130,"B9":131
        }
        
        #Tone data HI.
        self.notenum_hi = (0x10,0x10,0x10,0x10,0x10,0x10,0x10,0x10,0x10,0x10,0x10,0x10,0x10,0x10,0x18,0x18,0x18,0x18,0x18,0x20,0x20,0x20,0x20,0x28,0x11,0x11,0x19,0x19,0x19,0x19,0x19,0x21,0x21,0x21,0x21,0x29,0x12,0x12,0x1A,0x1A,0x1A,0x1A,0x1A,0x22,0x22,0x22,0x22,0x2A,0x13,0x13,0x1B,0x1B,0x1B,0x1B,0x1B,0x23,0x23,0x23,0x23,0x2B,0x14,0x14,0x1C,0x1C,0x1C,0x1C,0x1C,0x24,0x24,0x24,0x24,0x2C,0x15,0x15,0x1D,0x1D,0x1D,0x1D,0x1D,0x25,0x25,0x25,0x25,0x2D,0x16,0x16,0x1E,0x1E,0x1E,0x1E,0x1E,0x26,0x26,0x26,0x26,0x2E,0x17,0x17,0x1F,0x1F,0x1F,0x1F,0x1F,0x27,0x27,0x27,0x27,0x2F,0x10,0x10,0x18,0x18,0x18,0x18,0x18,0x20,0x20,0x20,0x20,0x28,0x11,0x11,0x19,0x19,0x19,0x19,0x10,0x1E)
        #Tone data LO.
        self.notenum_lo = (0x65,0x65,0x65,0x65,0x65,0x65,0x65,0x65,0x65,0x65,0x65,0x65,0x65,0x7A,0x11,0x29,0x42,0x5D,0x79,0x17,0x37,0x59,0x7D,0x22,0x65,0x7A,0x11,0x29,0x42,0x5D,0x79,0x17,0x37,0x59,0x7D,0x22,0x65,0x7A,0x11,0x29,0x42,0x5D,0x79,0x17,0x37,0x59,0x7D,0x22,0x65,0x7A,0x11,0x29,0x42,0x5D,0x79,0x17,0x37,0x59,0x7D,0x22,0x65,0x7A,0x11,0x29,0x42,0x5D,0x79,0x17,0x37,0x59,0x7D,0x22,0x65,0x7A,0x11,0x29,0x42,0x5D,0x79,0x17,0x37,0x59,0x7D,0x22,0x65,0x7A,0x11,0x29,0x42,0x5D,0x79,0x17,0x37,0x59,0x7D,0x22,0x65,0x7A,0x11,0x29,0x42,0x5D,0x79,0x17,0x37,0x59,0x7D,0x22,0x65,0x7A,0x11,0x29,0x42,0x5D,0x79,0x17,0x37,0x59,0x7D,0x22,0x65,0x7A,0x11,0x29,0x42,0x5D,0x65,0x5D)

        #Tone parameter byte order and how to make a byte data
        self.synth_data_map = {
            ##COMMON
            # [ 2]: NOP 000000 | Basic Octave 11
            "Basic Octave":                           {"BYTE":  2, "SELF_MASK": 0x03, "SHFT_LEFT": 0, "DATA_MASK": 0x00},

            # [ 3]:LFO 11 | NOP 000 | Algorithm 111
            "LFO":                                    {"BYTE":  3, "SELF_MASK": 0x03, "SHFT_LEFT": 6, "DATA_MASK": 0x07},
            "Algorithm":                              {"BYTE":  3, "SELF_MASK": 0x07, "SHFT_LEFT": 0, "DATA_MASK": 0xf8},

            ##OP1
            # [ 4]: OP1:Sustain Rate 1111 | Ignore Key Off 0 | Key Scale Sensitivity 111
            "Sustain Rate1":                          {"BYTE":  4, "SELF_MASK": 0x10, "SHFT_LEFT": 4, "DATA_MASK": 0x0f},
            "Ignore Key Off1":                        {"BYTE":  4, "SELF_MASK": 0x01, "SHFT_LEFT": 3, "DATA_MASK": 0xf7},
            "Key Scale Sensitivity1":                 {"BYTE":  4, "SELF_MASK": 0x07, "SHFT_LEFT": 0, "DATA_MASK": 0xf8},

            # [ 5]: OP1:Release Rate 1111 | Decay Rate 0000
            "Release Rate1":                          {"BYTE":  5, "SELF_MASK": 0x0f, "SHFT_LEFT": 4, "DATA_MASK": 0x0f},
            "Decay Rate1":                            {"BYTE":  5, "SELF_MASK": 0x0f, "SHFT_LEFT": 0, "DATA_MASK": 0xf0},

            # [ 6]: OP1:Attack Rate 1111 | Sustain Level 0000
            "Attack Rate1":                           {"BYTE":  6, "SELF_MASK": 0x0f, "SHFT_LEFT": 4, "DATA_MASK": 0x0f},
            "Sustain Level1":                         {"BYTE":  6, "SELF_MASK": 0x0f, "SHFT_LEFT": 0, "DATA_MASK": 0xf0},

            # [ 7]: OP1:Total Operator Level 111111 | Key Scale Level Sensivitiy 00
            "Total Operator Level1":                  {"BYTE":  7, "SELF_MASK": 0x3f, "SHFT_LEFT": 2, "DATA_MASK": 0x03},
            "Key Scale Level Sensivitiy1":            {"BYTE":  7, "SELF_MASK": 0x03, "SHFT_LEFT": 0, "DATA_MASK": 0xfc},

            # [ 8]: OP1:Depth Of Amp Modulation 111 | Enable Amp Modulation 0 | Depth Of Vibrate 111 | Enable Vibrate 0
            "Depth Of Amp Modulation1":               {"BYTE":  8, "SELF_MASK": 0x07, "SHFT_LEFT": 5, "DATA_MASK": 0x1f},
            "Enable Amp Modulation1":                 {"BYTE":  8, "SELF_MASK": 0x01, "SHFT_LEFT": 4, "DATA_MASK": 0xef},
            "Depth Of Vibrate1":                      {"BYTE":  8, "SELF_MASK": 0x07, "SHFT_LEFT": 1, "DATA_MASK": 0xf1},
            "Enable Vibrate1":                        {"BYTE":  8, "SELF_MASK": 0x01, "SHFT_LEFT": 0, "DATA_MASK": 0xfe},

                # [ 9]: OP1:Multi Control Magnification Frequency 1111 | Detune 0000
            "Multi Control Magnification Frequency1": {"BYTE":  9, "SELF_MASK": 0x0f, "SHFT_LEFT": 4, "DATA_MASK": 0x0f},
            "Detune1":                                {"BYTE":  9, "SELF_MASK": 0x0f, "SHFT_LEFT": 0, "DATA_MASK": 0xf0},

            # [10]: OP1:Wave Shape 11111 | FM Feedback Level 000
            "Wave Shape1":                            {"BYTE": 10, "SELF_MASK": 0x1f, "SHFT_LEFT": 3, "DATA_MASK": 0x07},
            "FM Feedback Level1":                     {"BYTE": 10, "SELF_MASK": 0x07, "SHFT_LEFT": 0, "DATA_MASK": 0xf8},

            ##OP2
            # [11]: OP2:Sustain Rate 1111 | Ignore Key Off 0 | Key Scale Sensitivity 111
            "Sustain Rate2":                          {"BYTE": 11, "SELF_MASK": 0x10, "SHFT_LEFT": 4, "DATA_MASK": 0x0f},
            "Ignore Key Off2":                        {"BYTE": 11, "SELF_MASK": 0x01, "SHFT_LEFT": 3, "DATA_MASK": 0xf7},
            "Key Scale Sensitivity2":                 {"BYTE": 11, "SELF_MASK": 0x07, "SHFT_LEFT": 0, "DATA_MASK": 0xf8},

            # [12]: OP2:Release Rate 1111 | Decay Rate 0000
            "Release Rate2":                          {"BYTE": 12, "SELF_MASK": 0x0f, "SHFT_LEFT": 4, "DATA_MASK": 0x0f},
            "Decay Rate2":                            {"BYTE": 12, "SELF_MASK": 0x0f, "SHFT_LEFT": 0, "DATA_MASK": 0xf0},

            # [13]: OP2:Attack Rate 1111 | Sustain Level 0000
            "Attack Rate2":                           {"BYTE": 13, "SELF_MASK": 0x0f, "SHFT_LEFT": 4, "DATA_MASK": 0x0f},
            "Sustain Level2":                         {"BYTE": 13, "SELF_MASK": 0x0f, "SHFT_LEFT": 0, "DATA_MASK": 0xf0},

            # [14]: OP2:Total Operator Level 111111 | Key Scale Level Sensivitiy 00
            "Total Operator Level2":                  {"BYTE": 14, "SELF_MASK": 0x3f, "SHFT_LEFT": 2, "DATA_MASK": 0x03},
            "Key Scale Level Sensivitiy2":            {"BYTE": 14, "SELF_MASK": 0x03, "SHFT_LEFT": 0, "DATA_MASK": 0xfc},

            # [15]: OP2:Depth Of Amp Modulation 111 | Enable Amp Modulation 0 | Depth Of Vibrate 111 | Enable Vibrate 0
            "Depth Of Amp Modulation2":               {"BYTE": 15, "SELF_MASK": 0x07, "SHFT_LEFT": 5, "DATA_MASK": 0x1f},
            "Enable Amp Modulation2":                 {"BYTE": 15, "SELF_MASK": 0x01, "SHFT_LEFT": 4, "DATA_MASK": 0xef},
            "Depth Of Vibrate2":                      {"BYTE": 15, "SELF_MASK": 0x07, "SHFT_LEFT": 1, "DATA_MASK": 0xf1},
            "Enable Vibrate2":                        {"BYTE": 15, "SELF_MASK": 0x01, "SHFT_LEFT": 0, "DATA_MASK": 0xfe},

            # [16]: OP2:Multi Control Magnification Frequency 1111 | Detune 0000
            "Multi Control Magnification Frequency2": {"BYTE": 16, "SELF_MASK": 0x0f, "SHFT_LEFT": 4, "DATA_MASK": 0x0f},
            "Detune2":                                {"BYTE": 16, "SELF_MASK": 0x0f, "SHFT_LEFT": 0, "DATA_MASK": 0xf0},

            # [17]: OP2:Wave Shape 11111 | FM Feedback Level 000
            "Wave Shape2":                            {"BYTE": 17, "SELF_MASK": 0x1f, "SHFT_LEFT": 3, "DATA_MASK": 0x07},
            "FM Feedback Level2":                     {"BYTE": 17, "SELF_MASK": 0x07, "SHFT_LEFT": 0, "DATA_MASK": 0xf8},

            ##OP3
            # [18]: OP3:Sustain Rate 1111 | Ignore Key Off 0 | Key Scale Sensitivity 111
            "Sustain Rate3":                          {"BYTE": 18, "SELF_MASK": 0x10, "SHFT_LEFT": 4, "DATA_MASK": 0x0f},
            "Ignore Key Off3":                        {"BYTE": 18, "SELF_MASK": 0x01, "SHFT_LEFT": 3, "DATA_MASK": 0xf7},
            "Key Scale Sensitivity3":                 {"BYTE": 18, "SELF_MASK": 0x07, "SHFT_LEFT": 0, "DATA_MASK": 0xf8},

            # [19]: OP3:Release Rate 1111 | Decay Rate 0000
            "Release Rate3":                          {"BYTE": 19, "SELF_MASK": 0x0f, "SHFT_LEFT": 4, "DATA_MASK": 0x0f},
            "Decay Rate3":                            {"BYTE": 19, "SELF_MASK": 0x0f, "SHFT_LEFT": 0, "DATA_MASK": 0xf0},

            # [20]: OP3:Attack Rate 1111 | Sustain Level 0000
            "Attack Rate3":                           {"BYTE": 20, "SELF_MASK": 0x0f, "SHFT_LEFT": 4, "DATA_MASK": 0x0f},
            "Sustain Level3":                         {"BYTE": 20, "SELF_MASK": 0x0f, "SHFT_LEFT": 0, "DATA_MASK": 0xf0},

            # [21]: OP3:Total Operator Level 111111 | Key Scale Level Sensivitiy 00
            "Total Operator Level3":                  {"BYTE": 21, "SELF_MASK": 0x3f, "SHFT_LEFT": 2, "DATA_MASK": 0x03},
            "Key Scale Level Sensivitiy3":            {"BYTE": 21, "SELF_MASK": 0x03, "SHFT_LEFT": 0, "DATA_MASK": 0xfc},

            # [22]: OP3:Depth Of Amp Modulation 111 | Enable Amp Modulation 0 | Depth Of Vibrate 111 | Enable Vibrate 0
            "Depth Of Amp Modulation3":               {"BYTE": 22, "SELF_MASK": 0x07, "SHFT_LEFT": 5, "DATA_MASK": 0x1f},
            "Enable Amp Modulation3":                 {"BYTE": 22, "SELF_MASK": 0x01, "SHFT_LEFT": 4, "DATA_MASK": 0xef},
            "Depth Of Vibrate3":                      {"BYTE": 22, "SELF_MASK": 0x07, "SHFT_LEFT": 1, "DATA_MASK": 0xf1},
            "Enable Vibrate3":                        {"BYTE": 22, "SELF_MASK": 0x01, "SHFT_LEFT": 0, "DATA_MASK": 0xfe},

            # [23]: OP3:Multi Control Magnification Frequency 1111 | Detune 0000
            "Multi Control Magnification Frequency3": {"BYTE": 23, "SELF_MASK": 0x0f, "SHFT_LEFT": 4, "DATA_MASK": 0x0f},
            "Detune3":                                {"BYTE": 23, "SELF_MASK": 0x0f, "SHFT_LEFT": 0, "DATA_MASK": 0xf0},

            # [24]: OP3:Wave Shape 11111 | FM Feedback Level 000
            "Wave Shape3":                            {"BYTE": 24, "SELF_MASK": 0x1f, "SHFT_LEFT": 3, "DATA_MASK": 0x07},
            "FM Feedback Level3":                     {"BYTE": 24, "SELF_MASK": 0x07, "SHFT_LEFT": 0, "DATA_MASK": 0xf8},

            ##OP4
            # [25]: OP4:Sustain Rate 1111 | Ignore Key Off 0 | Key Scale Sensitivity 111
            "Sustain Rate4":                          {"BYTE": 25, "SELF_MASK": 0x10, "SHFT_LEFT": 4, "DATA_MASK": 0x0f},
            "Ignore Key Off4":                        {"BYTE": 25, "SELF_MASK": 0x01, "SHFT_LEFT": 3, "DATA_MASK": 0xf7},
            "Key Scale Sensitivity4":                 {"BYTE": 25, "SELF_MASK": 0x07, "SHFT_LEFT": 0, "DATA_MASK": 0xf8},

            # [26]: OP4:Release Rate 1111 | Decay Rate 0000
            "Release Rate4":                          {"BYTE": 26, "SELF_MASK": 0x0f, "SHFT_LEFT": 4, "DATA_MASK": 0x0f},
            "Decay Rate4":                            {"BYTE": 26, "SELF_MASK": 0x0f, "SHFT_LEFT": 0, "DATA_MASK": 0xf0},

            # [27]: OP4:Attack Rate 1111 | Sustain Level 0000
            "Attack Rate4":                           {"BYTE": 27, "SELF_MASK": 0x0f, "SHFT_LEFT": 4, "DATA_MASK": 0x0f},
            "Sustain Level4":                         {"BYTE": 27, "SELF_MASK": 0x0f, "SHFT_LEFT": 0, "DATA_MASK": 0xf0},

            # [28]: OP4:Total Operator Level 111111 | Key Scale Level Sensivitiy 00
            "Total Operator Level4":                  {"BYTE": 28, "SELF_MASK": 0x3f, "SHFT_LEFT": 2, "DATA_MASK": 0x03},
            "Key Scale Level Sensivitiy4":            {"BYTE": 28, "SELF_MASK": 0x03, "SHFT_LEFT": 0, "DATA_MASK": 0xfc},

            # [29]: OP4:Depth Of Amp Modulation 111 | Enable Amp Modulation 0 | Depth Of Vibrate 111 | Enable Vibrate 0
            "Depth Of Amp Modulation4":               {"BYTE": 29, "SELF_MASK": 0x07, "SHFT_LEFT": 5, "DATA_MASK": 0x1f},
            "Enable Amp Modulation4":                 {"BYTE": 29, "SELF_MASK": 0x01, "SHFT_LEFT": 4, "DATA_MASK": 0xef},
            "Depth Of Vibrate4":                      {"BYTE": 29, "SELF_MASK": 0x07, "SHFT_LEFT": 1, "DATA_MASK": 0xf1},
            "Enable Vibrate4":                        {"BYTE": 29, "SELF_MASK": 0x01, "SHFT_LEFT": 0, "DATA_MASK": 0xfe},

            # [30]: OP4:Multi Control Magnification Frequency 1111 | Detune 0000
            "Multi Control Magnification Frequency4": {"BYTE": 30, "SELF_MASK": 0x0f, "SHFT_LEFT": 4, "DATA_MASK": 0x0f},
            "Detune4":                                {"BYTE": 30, "SELF_MASK": 0x0f, "SHFT_LEFT": 0, "DATA_MASK": 0xf0},

            # [31]: OP4:Wave Shape 11111 | FM Feedback Level 000
            "Wave Shape4":                            {"BYTE": 31, "SELF_MASK": 0x1f, "SHFT_LEFT": 3, "DATA_MASK": 0x07},
            "FM Feedback Level4":                     {"BYTE": 31, "SELF_MASK": 0x07, "SHFT_LEFT": 0, "DATA_MASK": 0xf8}
        }
        
        # Sustain pedal control
        self.NO_SUSTAIN      = 0                              # Sustain pedal is released
        self.WILL_BE_SUSTAIN = 1                              # Sustain pedal was pressed while note on
        self.IN_SUSTAIN      = 2                              # Note off but sustain pedal is pressed
        self.sustain_pressed = -1;                            # True while sustain pedal is pressed, otherwise False

        # YMF825 Voices.
        self.VOICES = 16                                      # Maximum voices
        self.synth_voices  = [""] * self.VOICES               # Playing note like "C4" or "C4#" each voice, voices are spearated 4-timbres.
        self.synth_volumes = [0] * self.VOICES                # Playing note volume (0..31) each voice
        self.synth_sustain = [self.NO_SUSTAIN] * self.VOICES  # Sustain pedal status for each voice
#        self.synth_sounds = [[[0]*36]] * self.VOICES          # Sound parameters each voice
        self.synth_sounds = [bytearray(36)] * self.VOICES       # Sound parameters each voice
        self.synth_sel_voices = list(range(0,self.VOICES+1))  # Number of voices to assign each timbre portion
        self.synth_sel_volume = list(range(0,32))             # Voice volume (0..31)

        # Sounds (YMF825 sound parameter).
        self.TONES = 20                                  # Maximum tones
        self.PRESET_TONES = 2                            # TONE 0 and 1 is preset tones, can NOT edit
        self.synth_edit_tone = 0
        self.synth_tone_names = ["NoName"] * self.TONES
        self.synth_tones = [[0,0x80 + self.VOICES]+[0]*30+[0x80,0x03,0x81,0x80]] * self.TONES

        # Multi-Timbre.
        self.TIMBRES = 10                                   # Maximum timbres
        self.TIMBRE_PORTIONS = 4                            # Maximum portions in timbre
        self.synth_play_timbre = 0                          # Playing timbre index
        self.synth_timbre_names = ["NoName"] * self.TIMBRES # Timbre names list
        self.synth_timbres = [[                             # YMF825 voice number (from-to) and its tone index for each timbre [Timber List][Timber Postion][from to]
                                {"voice_from":  0, "voice_to": 15, "tone": 0, "volume": 31},
                                {"voice_from": -1, "voice_to": -1, "tone": 0, "volume":  0},
                                {"voice_from": -1, "voice_to": -1, "tone": 0, "volume":  0},
                                {"voice_from": -1, "voice_to": -1, "tone": 0, "volume":  0}
                             ]] * self.TIMBRES

        # Equalizer settings
        self.EQUALIZERS = 10
        self.synth_selected_equalizer = 1
        self.synth_equalizer_names = ["NoName"] * self.EQUALIZERS
        self.synth_equalizer_settings = [[
                                            {"ceq0": 1, "ceq1": 0, "ceq2": 0, "ceq3": 0, "ceq4": 0},
                                            {"ceq0": 1, "ceq1": 0, "ceq2": 0, "ceq3": 0, "ceq4": 0},
                                            {"ceq0": 1, "ceq1": 0, "ceq2": 0, "ceq3": 0, "ceq4": 0}
                                        ]] * self.EQUALIZERS

        # Files
        self.tone_name_file = file_tone_name
        self.tone_param_file= file_tone_param
        self.timbre_name_file = file_timbre_name
        self.timbre_param_file = file_timbre_param
        self.equalizer_name_file = file_equalizer_name
        self.equalizer_param_file = file_equalizer_param
        self.file_encode = file_encode
        
        # Equalizer parameters buffer (address + 15bytes)
        self.equalizer_ceq = bytearray(16)


    # LED indicator.
    #   onoff:: True:turn on, False: turn off
    def led_turn( self, onoff ):
        self.led_indicator.value(1 if onoff else 0)


    # Wait timer.
    #   msec:: Waite time in milli-seconds
    def delay( self, msec ):
        time.sleep( msec/1000 )


    # Set SPI Slave Select Pin (CE0).
    #   pinv:: GPIO.HIGH: not-select, GPIO.LOW: select
    def chip_select( self, sel ):
        self.spi_cs.value(0 if sel else 1)


    # Write byte array data to SPI.
    #   addr:: SPI register address
    #   data_array: byte data in array
    def spi_write( self, addr, data_array ):
        self.chip_select(True)
        data_array[0] = addr
        self.spi.write(data_array)
        self.chip_select(False)


    # Write one byte data to SPI.
    #   addr:: SPI register address
    #   byte_data: one byte data
    def spi_write_byte( self, addr, byte_data ):
        spi_byte_data = bytearray([addr, byte_data])
        self.chip_select(True)
        self.spi.write(spi_byte_data)
        self.chip_select(False)


    # Set YMF825 Chanel.
    def set_chanel( self ):
        self.spi_write_byte( 0x0F, 0x30 )       # Note on
        self.spi_write_byte( 0x10, 0x71 )       # Chanel volume
        self.spi_write_byte( 0x11, 0x00 )       # XVB
        self.spi_write_byte( 0x12, 0x08 )       # FRAC
        self.spi_write_byte( 0x13, 0x00 )       # FRAc


    # Note on (play a note).
    # NOTICE:: Never call this directory, use play_by_scale() or play_by_timbre_scale().
    #   fnumh, fnuml:: 2byte data to play, byte data for a note is in notenum_hi[note] and notenum_lo[note].
    def note_on( self, voice, notenum_h, notenum_l, volume = 0x7c ):
#        print("NOTE ON VOLUME =", str(volume))
        # Send note on to YMF825
        self.spi_write_byte( 0x0B, voice & 0x0f )
        self.spi_write_byte( 0x0C, volume & 0x7c )
        self.spi_write_byte( 0x0D, notenum_h )
        self.spi_write_byte( 0x0E, notenum_l )
        self.spi_write_byte( 0x0F, 0x40 | (voice&0x0f) )

        # LED
        self.led_turn( True )


    # Note off.
    #   Turn off the note playing.
    def note_off( self, voice, volume = 0x54 ):
        if self.synth_voices[voice] in self.note_dict:
            s = self.get_scale_number( self.synth_voices[voice] )
            print("STOP VOICE, SCALE:", voice,s)
            self.spi_write_byte( 0x0B, voice & 0x0f )
            self.spi_write_byte( 0x0C, volume & 0x7c )
            self.spi_write_byte( 0x0D, self.notenum_hi[s] )
            self.spi_write_byte( 0x0E, self.notenum_lo[s] )
            self.spi_write_byte( 0x0F, 0x00 | (voice&0x0f) )
        else:
            print("UNKNOWN STOP VOICE:[", voice, "]")
            
        # LED
        self.led_turn(False)


    # Get scale number in fnum_hi nd lo.
    #   scale:: "C4", "D5#", "F2", "E3b" and so on. From "C0" to "G9".
    #
    #   RETURN:: scale number(index) in fnum_hi nd lo.
    def get_scale_number( self, scale ):
        return self.note_dict[scale]


    # Play by a scale name, play time and rest time.
    # Use 0-voice only.
    #   scale:: "C4", "D5#", "F2", and so on. From "C0" to "G9".
    #   play:: note on time(msec).
    #   rest:: note off time(msec) after playing the note.
    def play_by_scale( self, scale, play, rest ):
        s = self.get_scale_number(scale)
        if s <= 127:
            print("PLAY:", scale, "=", s, " ", play, "_", rest, "//")
            self.synth_voices[0] = scale
            self.note_on( 0, self.notenum_hi[s], self.notenum_lo[s] )
            self.delay( play )
            self.note_off( 0 )
            self.delay( rest )
        else:
            print("Unknown scale:", scale)


    # Get voice number playing new note in timbre.
    #   timbre_portion:: Multi-Timbre index (0..3).
    #   scale:: "C4", "D5#", "F2", and so on. From "C0" to "G9".
    #   play:: True: find a voice not playing, False: find the scale only.
    #
    #   RETURN:: voice number
    def get_voice_in_timbre( self, timbre_portion, scale, play=True ):
        v = -1
        if timbre_portion >= 0 and timbre_portion < self.TIMBRE_PORTIONS and self.synth_timbres[self.synth_play_timbre][timbre_portion]["voice_from"] >= 0:
            for i in range(self.synth_timbres[self.synth_play_timbre][timbre_portion]["voice_from"], self.synth_timbres[self.synth_play_timbre][timbre_portion]["voice_to"]+1):
                if self.synth_voices[i] == scale:
                    return i
                if play and self.synth_voices[i] == "":
                    v = i

        #There is no voice not playing, use "first-voice" in the tmbre
        if v == -1 and play:
            v = self.synth_timbres[self.synth_play_timbre][timbre_portion]["voice_to"]
            self.note_off(v)

        return v


    #Get a note string ("C4", "D#3", ...) of note number (60-->"C4")
    # scale:: note number
    #
    # String of the note
    def get_note_scale(self, scale):
        return self.note_name[scale]


    # Play by a scale name, call stop_by_timbre_scale() to turn off the scale.
    #   timbre_portion:: Multi-Timbre portion index (0..TIMBRE_PORTIONS)
    #   scale:: "C4", "D5#", "F2", and so on. From "C0" to "G9".
    #
    #   RETURN:: voice number
    def play_by_timbre_scale( self, timbre_portion, scale ):
        v = self.get_voice_in_timbre( timbre_portion, scale, True )
        if v >= 0 and self.synth_voices[v] != scale:
            s = self.get_scale_number(scale)
    
            if s <= 127:
                volume = self.synth_timbres[self.synth_play_timbre][timbre_portion]["volume"]
                print("PLAY:", self.synth_play_timbre, self.synth_timbre_names[self.synth_play_timbre], timbre_portion, self.synth_tone_names[self.synth_timbres[self.synth_play_timbre][timbre_portion]["tone"]], ":", scale, "=", s, v, "vol =", volume)
                self.note_on( v, self.notenum_hi[s], self.notenum_lo[s], volume << 2 )
                self.synth_voices[v] = scale
                self.synth_volumes[v] = volume
                        
                # Sustain pedal
                if self.sustain_pressed == timbre_portion:
                    self.synth_sustain[v] = self.WILL_BE_SUSTAIN

#            print("VOICES=",synth_voices)
            else:
                print("Unknown play scale:", scale)
        else:
            print("No start voice:", self.synth_play_timbre, timbre_portion, scale)

        return v


    # Play by a scale name, call stop_by_timbre_scale() to turn off the scale.
    #   timbre_portion:: Multi-Timbre portion index (0..TIMBRE_PORTIONS)
    #   scale:: "C4", "D5#", "F2", and so on. From "C0" to "G9".
    #
    #   RETURN:: voice number
    def play_by_timbre_scale_velocity( self, timbre_portion, scale, velocity ):
        v = self.get_voice_in_timbre( timbre_portion, scale, True )
        if v >= 0 and self.synth_voices[v] != scale:
            s = self.get_scale_number(scale)
    
            if s <= 127:
                # Inerite sustain pedal if the timbre portion is changed
                if self.sustain_pressed != -1:
                    self.sustain_pressed = timbre_portion
                
                # Note on
                volume = self.synth_timbres[self.synth_play_timbre][timbre_portion]["volume"]
                volume = math.floor(volume * velocity / 127)
                print("PLAY:", self.synth_play_timbre, self.synth_timbre_names[self.synth_play_timbre], timbre_portion, self.synth_tone_names[self.synth_timbres[self.synth_play_timbre][timbre_portion]["tone"]], ":", scale, "=", s, v, "vol =", volume)
                self.note_on( v, self.notenum_hi[s], self.notenum_lo[s], volume << 2 )
                self.synth_voices[v] = scale
                self.synth_volumes[v] = volume
                        
                # Sustain pedal
                if self.sustain_pressed == timbre_portion:
                    self.synth_sustain[v] = self.WILL_BE_SUSTAIN

#            print("VOICES=",synth_voices)
            else:
                print("Unknown play scale:", scale)
        else:
            print("No start voice:", self.synth_play_timbre, timbre_portion, scale)

        return v


    #  timbre_portion:: Multi-Timbre portion index (0..TIMBRE_PORTIONS)
    #  scale:: 60 = "C4", "From "C0" to "G9".
    #
    #  RETURN:: voice number
    def play_by_timbre_note(self, timbre_portion, scale, velocity):
        return self.play_by_timbre_scale_velocity(timbre_portion, self.note_name[scale], velocity)
    

    # Stop a scale in the timbre.
    #   timbre_portion: Multi-Timbre portion index (0..TIMBRE_PORTIONS)
    #   scale:: "C4", "D5#", "F2", and so on. From "C0" to "G9".
    def stop_by_timbre_scale( self, timbre_portion, scale ):
        v = self.get_voice_in_timbre( timbre_portion, scale, False )
    
        if v >= 0:
            volume = self.synth_timbres[self.synth_play_timbre][timbre_portion]["volume"]
            volume = self.synth_volumes[v]
            
            # Sustail pedal
            if self.synth_sustain[v] == self.WILL_BE_SUSTAIN:
                print("SUSTAIN:", timbre_portion, scale, "=", v, "vol =", volume)
                self.synth_sustain[v] = self.IN_SUSTAIN

            # Sustail pedal is released
            else:
                print("STOP:", timbre_portion, scale, "=", v, "vol =", volume)
                self.note_off( v, volume << 2 )
                self.synth_voices[v] = ""
                
#        print("VOICES=", synth_voices)
        else:
            print("Unknown stop voice:", self.synth_play_timbre, timbre_portion, scale)


    #Stop a scale in the timbre.
    #  timbre_portion: Multi-Timbre portion index (0..TIMBRE_PORTIONS)
    #  scale:: 60 = "C4", "From "C0" to "G9".
    def stop_by_timbre_note(self, timbre_portion, scale):
        self.stop_by_timbre_scale(timbre_portion, self.note_name[scale])


    #Set sutain pedal status
    #  timbre_portion: Multi-Timbre portion index (0..TIMBRE_PORTIONS)
    #  status:: True=Sutain pedal pressed, False=released.
    def sustain_pedal(self, timbre_portion, status):
        self.sustain_pressed = timbre_portion if status else -1;

        # Sustain pedal was pressed --> set sustain to playing voice in the timbre portion
        if status:
            for v in list(range(self.synth_timbres[self.synth_play_timbre][timbre_portion]["voice_from"], self.synth_timbres[self.synth_play_timbre][timbre_portion]["voice_to"]+1)):
                if self.synth_voices[v] != "":
                    self.synth_sustain[v] = self.WILL_BE_SUSTAIN
                    print("WILL_BE_SUSTAIN:", self.synth_voices[v])
        
        # Sustain pedal was released --> note off the notes in sustain mode (all timbres)
        else:
            for tp in list(range(0, self.TIMBRE_PORTIONS)):
                for v in list(range(self.synth_timbres[self.synth_play_timbre][tp]["voice_from"], self.synth_timbres[self.synth_play_timbre][tp]["voice_to"]+1)):
                    if self.synth_voices[v] != "":
                        if self.synth_sustain[v] == self.IN_SUSTAIN:
                            self.stop_by_timbre_scale(tp, self.synth_voices[v])
                            print("STOP SUSTAIN:", self.synth_voices[v])
                    
                        self.synth_sustain[v] = self.NO_SUSTAIN
        

    # Send sound data to YMF825.
    #   timbre_portion: Multi-Timbre portion index (0..TIMBRE_PORTIONS)
    def send_sound_to_YMF825( self, timbre ):
        all_sound_param = bytearray(self.synth_sounds[0][0:32])         # address + voices + prams
        for v in range(1,self.VOICES):                       # params * VOICES
            all_sound_param += bytearray(self.synth_sounds[v][2:32])
        all_sound_param += bytearray(self.synth_sounds[0][32:])         # trailer

        #Burst write mode
        print("YMF825 Burst write mode: ", timbre)
        self.spi_write_byte( 0x08, 0xF6 )
        self.delay(20)
        self.spi_write_byte( 0x08, 0x00 )

        #Write tone data to YMF825 FIFO.
        print("Write timbre tone data to YMF825:", timbre)
#    print("YMF825 PARAM:", all_sound_param)
        self.spi_write( 0x07, all_sound_param )


    # Get Synthesizer data map
    def get_synth_data_map( self ):
        return self.synth_data_map


    # Get Synthesizer tone names list
    def get_synth_tone_names( self ):
        return self.synth_tone_names


    # Get Synthesizer timbre names list
    def get_synth_timbre_names( self ):
        return self.synth_timbre_names


    # Get selected equalizer
    def get_selected_equalizer( self ):
        return self.synth_selected_equalizer


    # Get Synthesizer equalizer names list
    def get_synth_equalizer_names( self ):
        return self.synth_equalizer_names


    # Get synthesizer voices list
    def get_synth_sel_voices( self ):
        return self.synth_sel_voices


    # Get synthesizer volume list
    def get_synth_sel_volume( self ):
        return self.synth_sel_volume


    # Get playing timbre index
    def get_synth_play_timbre( self ):
        return self.synth_play_timbre


    # Set playing timbre index
    def set_synth_play_timbre( self, timbre ):
        self.synth_play_timbre = timbre


    # Get timbre voice from
    def get_timbre_voice_from( self, timbre, portion ):
        return self.synth_timbres[timbre][portion]["voice_from"]


    # Get timbre voice to
    def get_timbre_voice_to( self, timbre, portion ):
        return self.synth_timbres[timbre][portion]["voice_to"]


    # Get timbre voice from
    def get_playing_timbre_voice_from( self, portion ):
        return self.synth_timbres[self.synth_play_timbre][portion]["voice_from"]


    # Get timbre voice to
    def get_playing_timbre_voice_to( self, portion ):
        return self.synth_timbres[self.synth_play_timbre][portion]["voice_to"]


    # Get timbre voice tone
    def get_timbre_tone( self, timbre, portion ):
        return self.synth_timbres[timbre][portion]["tone"]


    # Get editing tone index
    def get_synth_edit_tone( self ):
        return self.synth_edit_tone


    # Get editing tone index
    def set_synth_edit_tone( self, tone ):
        self.synth_edit_tone = tone


    # Get
    def get_playing_timbre_tone( self, portion ):
        return self.synth_timbres[self.synth_play_timbre][portion]["tone"]


    # Set timbre portion tone
    def set_timbre_portion_tone( self, timbre, portion, tone ):
        self.synth_timbres[timbre][portion]["tone"] = tone


    # Set timbre portion volume
    def set_timbre_portion_volume( self, timbre, portion, volume ):
        self.synth_timbres[timbre][portion]["volume"] = volume


    # Get timbre portion volume
    def get_timbre_volume( self, timbre, portion ):
        return self.synth_timbres[timbre][portion]["volume"]


    # Get timbre portion volume
    def get_playing_timbre_volume( self, portion ):
        return self.synth_timbres[self.synth_play_timbre][portion]["volume"]


    # Set timbre portion volume
    def set_playing_timbre_volume( self, portion, volume ):
        self.synth_timbres[self.synth_play_timbre][portion]["volume"] = volume


    # Set equalizer
    #   eql:: Equalizer number (0..2)
    #   ceq#:: ceq-eql-#
    def set_equalizer( self, eql, ceq0 = 1.0, ceq1 = 0.0, ceq2 = 0.0, ceq3 = 0.0, ceq4 = 0.0 ):

        def dec2bin_frac( dec, sign = False, digits=54 ):
#            dec=Decimal(str(dec))
            dec=float(str(dec))
            mantissa=''
            nth=0
            first=0
            rb=False
            while dec:
                if dec  >= 1:
#                    mantissa += '1'
                    mantissa += '1' if not sign else '0'
                    dec = dec -1
                    if first==0:
                        first=nth
                else:
                    if nth!=0:
#                        mantissa += '0'
                        mantissa += '0' if not sign else '1'
                    else:
                        mantissa += '0.'
                dec*=2
                nth+=1
                if nth-first==digits:
                    if dec != 0:
                        rb=True
                    break

            carry = False
            if sign:
                print("SIGN BFR:", mantissa)
                revs = ""
                lman = len(mantissa)
                for b in range(1,lman-1):
                    if mantissa[-b] == "0":
                        revs = "1" + revs
                        if b != lman-2:
                            revs = mantissa[2:lman-b] + revs

                        break
                    else:
                        revs = "0" + revs
                        if b == lman-2:
                            carry = True

                mantissa = "0." + revs
                print("SIGN AFT:", mantissa, carry)

            return mantissa,carry,rb

        # Make CEQ# bytes data
        def make_ceq_bytes( ceq_num, ceq ):
            ceq_num = ceq_num * 3 + 1

            if ceq < 0.0:
                sign = True
                self.equalizer_ceq[ceq_num] = 0x80
                ceq = -ceq
                ceq_int = ( ~int(ceq) ) & 0x07
                ceq_frc = ceq - int(ceq)
            else:
                sign = False
                self.equalizer_ceq[ceq_num+1] = 0x00
                ceq_int = int(ceq) & 0x07
                ceq_frc = ceq - int(ceq)

            if ceq_frc != 0.0:
                mantissa,carry,rb = dec2bin_frac( ceq_frc, sign, 23 )
                if carry:
                    ceq_int += 1

                print("EQUALIZER BITS and CARRY = INT:", mantissa, carry, "=", ceq_int)
                self.equalizer_ceq[ceq_num] = self.equalizer_ceq[ceq_num] | ( ceq_int << 4 )
                print("FRC:: CEQ INT SHIFT ARRAY FRAC=", ceq, ceq_int, ( ceq_int << 4 ), self.equalizer_ceq[ceq_num], ceq_frc)
                for b in range(2,len( mantissa )):
                    print("BIT:", b, "=", mantissa[b])
                    if mantissa[b] == "1":
                        if   b <=  5:       #  2.. 5
                            self.equalizer_ceq[ceq_num  ] = self.equalizer_ceq[ceq_num  ] | ( 0x01 << ( 5-b) )
                        elif b <= 13:       #  6..13
                            self.equalizer_ceq[ceq_num+1] = self.equalizer_ceq[ceq_num+1] | ( 0x01 << (13-b) )
                        elif b <= 21:       # 14..21
                            self.equalizer_ceq[ceq_num+2] = self.equalizer_ceq[ceq_num+2] | ( 0x01 << (21-b) )

            else:
                if sign:
                    ceq_int += 1

                self.equalizer_ceq[ceq_num] = self.equalizer_ceq[ceq_num] | ( ceq_int << 4 )
                print("INT:: CEQ INT SHIFT ARRAY FRAC=", ceq, ceq_int, ( ceq_int << 4 ), self.equalizer_ceq[ceq_num], ceq_frc)

            print("EQL::", self.equalizer_ceq[ceq_num], self.equalizer_ceq[ceq_num+1], self.equalizer_ceq[ceq_num+2])

        # Clear CEQ bytes data
        for b in range(15):
            self.equalizer_ceq[b] = 0

        # Make CEQ0 bytes data
        make_ceq_bytes( 0, ceq0 )
        make_ceq_bytes( 1, ceq1 )
        make_ceq_bytes( 2, ceq2 )
        make_ceq_bytes( 3, ceq3 )
        make_ceq_bytes( 4, ceq4 )

        #Burst write mode and all key notes off
#    print("EDITOR: YMF825 Burst write mode.")
        self.spi_write_byte( 0x08, 0xF6 )
        self.delay(20)
        self.spi_write_byte( 0x08, 0x00 )

        #Write tone data to YMF825 FIFO.
#    print("EDITOR: Write sound data to YMF825.")
        print("EQUALIZER", eql, ":", list(self.equalizer_ceq))
        self.spi_write( 32 + eql, bytearray(list(self.equalizer_ceq)) )


    # Set timbre voice range.
    #   timbre:: Timbre index (0..TIMBRES-1)
    #   timbre_portion:: Timbre portion index(0..TIMBRE_PORTIONS-1) in the timbre
    #   vfrom:: vioce from
    #   vto  :: voice to
    def set_timbre_voice_range( self, timbre, timbre_portion, vfrom, vto ):
        if vfrom < 0 or vto < 0 or vfrom >= self.VOICES or vto >= self.VOICES:
            vfrom = -1
            vto = -1

        if vfrom <= vto:
            self.synth_timbres[timbre][timbre_portion]["voice_from"] = vfrom
            self.synth_timbres[timbre][timbre_portion]["voice_to"] = vto


    # Set timbre portion sound (but not send it to YMF825).
    #   timbre:: Timbre index (0..TIMBRES-1)
    #   timbre_portion:: timbre index (0..TIMBRE_PORTIONS)
    def set_timbre_tone( self, timbre, timbre_portion ):
        vs = self.synth_timbres[self.synth_play_timbre][timbre_portion]["voice_from"];
        vt = self.synth_timbres[self.synth_play_timbre][timbre_portion]["voice_to"];
        if vs >=0 and vs <= vt:
            print("SET TIMBER PORTION TONE", timbre, timbre_portion, self.synth_timbres[self.synth_play_timbre][timbre_portion]["tone"], ":", vs, vt )
            for v in range(vs,vt+1):
                self.synth_sounds[v] = self.synth_tones[self.synth_timbres[self.synth_play_timbre][timbre_portion]["tone"]].copy()


    # Set timber sound and send it to YMF825.
    #   timbre:: Timbre index (0..TIMBRES-1)
    def set_timbre_tones( self, timbre ):
        for p in range(self.TIMBRE_PORTIONS):
            self.set_timbre_tone( timbre, p )
#        print("TIMBRE TONE:", "tmbtone_T" + str(p))
#        gui_timbre_pane["tmbtone_T" + str(p)]["object"].set( synth_tone_names[synth_timbres[synth_play_timbre][p]["tone"]] )

        self.send_sound_to_YMF825( timbre )


    # Rename tone name
    #   tone:: Tone index (0..TONES-1)
    #   name:: name to rename
    #
    #   RETURN:: ("INFO|ERROR","TONE","message-string")
    def rename_tone( self, tone, name ):
        if tone == 0:
            self.synth_tone_names[tone] = "EDITING"
            return ("","TONE","")

        name = re.sub( '^ {1,}', "", name )
        name = re.sub( ' {1,}$', "", name )
        print("RENAME TONE", self.synth_tone_names[tone], "-->", name, ":", self.synth_tone_names.count( name ))

        if   name == "":
            return ( "ERROR", "TONE", "Illegal tone name." )
    
        elif self.synth_tone_names.count( name ) == 0:
            self.synth_tone_names[tone] = name
#        set_playing_timbre( synth_play_timbre )
            return ( "INFO", "TONE", "Tone name was renamed." )

        elif self.synth_tone_names.index( name ) != tone:
            return ( "ERROR", "TONE", "Same tone name already exists." )

        else:
            self.synth_tone_names[tone] = name

        return ("","TONE","")


    # Rename timbre name
    #   timbre:: Timbre index (0..TIMBRES-1)
    #   name:: name to rename
    #
    #   RETURN:: ("INFO|ERROR","TIMBRE","message-string")
    def rename_timbre( self, timbre, name ):
        name = re.sub( '^ {1,}', "", name )
        name = re.sub( ' {1,}$', "", name )
        print("RENAME TIMBER", self.synth_timbre_names[timbre], "-->", name, ":", self.synth_timbre_names.count( name ))

        if   timbre == 0:
            return ( "ERROR", "TIMBER", "Can't rename EDITING timbre." )

        elif name == "":
            return ( "ERROR", "TIMBER", "Illegal timbre name." )

        elif self.synth_timbre_names.count( name ) == 0:
            self.synth_timbre_names[timbre] = name
            return ( "INFO", "TIMBER", "Timbre name was renamed." )

        elif self.synth_timbre_names.index( name ) != timbre:
            return ( "ERROR", "TIMBER", "Same timbre name already exists." )

        return ("","TIMBRE","")


    # Rename euqalizer name
    def rename_equalizer( self, eql, name ):
        name = re.sub( '^ {1,}', "", name )
        name = re.sub( ' {1,}$', "", name )
        print("RENAME EQUALIZER", self.synth_equalizer_names[eql], "-->", name, ":", self.synth_equalizer_names.count( name ))

        if   ( eql == 0 or eql == 1 ) and self.synth_equalizer_names[eql] != name:
            return ( "ERROR", "EQUALIZER", "Can't rename EDITING or ALL PATH equalizer." )

        elif name == "":
            return ( "ERROR", "EQUALIZER", "Illegal equalizer name." )

        elif self.synth_equalizer_names.count( name ) == 0:
            self.synth_equalizer_names[eql] = name
            return ( "INFO", "EQUALIZER", "Equalizer name was renamed." )

        elif eql >= 2 and self.synth_equalizer_names.index( name ) != eql:
            return ( "ERROR", "EQUALIZER", "Same equalizer name already exists." )

        return ("","EQUALIZER","")


    # Get a editing tone parameters as hash
    #   sound_prm:: byte array of YMF825 sound parameter
    #   RETURN:: One sound parameter as hash
    def get_editing_tone( self, sound_prm ):
        paramHash = {"Address": 0, "Voices": sound_prm[ 1] - 0x80}
    
        for (param,proc) in self.synth_data_map.items():
            byte_order = proc["BYTE"]
            self_mask  = proc["SELF_MASK"]
            shift_left = proc["SHFT_LEFT"]
#        data_mask  = proc["DATA_MASK"]
            paramHash[param] = (sound_prm[byte_order] >> shift_left ) & self_mask

        return paramHash


    # Set one sound parameters to all voices.
    # This function is for sound editor.
    #   paramHash:: Tone parameter to edit as a hash
    def set_editing_tone( self, paramHash ):
#    print("Set begin:", self.sound_param)

        #HED: 0,0x81,
        ## [ 0]: Register Address (constant)
        self.sound_param[0] = 0

        ## [ 1]: Header 0x80 + voices(=16 constant)
        self.sound_param[1] = 0x80 + self.VOICES

        for (param,val) in paramHash.items():
            if param in self.synth_data_map:
#            print("Edit:", param, "=", val)
                byte_order = self.synth_data_map[param]["BYTE"]
                self_mask  = self.synth_data_map[param]["SELF_MASK"]
                shift_left = self.synth_data_map[param]["SHFT_LEFT"]
                data_mask  = self.synth_data_map[param]["DATA_MASK"]
                self.sound_param[byte_order] = (self.sound_param[byte_order] & data_mask) | ((val & self_mask) << shift_left)

            else:
                print("UNKNOWN PARAMETER NAME:", param, "=", val)

        # TRAILER CODES: 0x80,0x03,0x81,0x80
        self.sound_param[32]=0x80
        self.sound_param[33]=0x03
        self.sound_param[34]=0x81
        self.sound_param[35]=0x80

        #Burst write mode and all key notes off
#    print("EDITOR: YMF825 Burst write mode.")
        self.spi_write_byte( 0x08, 0xF6 )
        self.delay(20)
        self.spi_write_byte( 0x08, 0x00 )

        #Write tone data to YMF825 FIFO.
#    print("EDITOR: Write sound data to YMF825.")
#    print("Set end:", sound_param)
        self.spi_write( 0x07, bytearray(self.sound_param) )
#    print("Write end:", sound_param)


    # Save edited sound parameters to a tone data
    # The sound parameters in self.sound_param is set by self.set_editing_tone()
    #   tone: Tone index.
    def save_edited_data_to_tone( self, tone ):
        self.synth_tones[tone] = self.sound_param.copy()
    #    print("Save:", sound_param)


    # Copy a tone to the sound parameters to edit
    #   tone: Tone index.
    def copy_tone_data_for_edit( self, tone ):
        self.sound_param = self.synth_tones[tone].copy()
    #    print("Edit:", sound_param)
        return self.get_editing_tone( self.sound_param )


    # Set equalizer
    #   eql:: Equalizer setting number (0..EQUALIZERS-1)
    def set_synth_equalizer( self, eql ):
        if eql >= 0 and eql < self.EQUALIZERS:
            self.synth_selected_equalizer = eql
            for e in range(3):
                self.set_equalizer( e, self.synth_equalizer_settings[eql][e]["ceq0"], self.synth_equalizer_settings[eql][e]["ceq1"], self.synth_equalizer_settings[eql][e]["ceq2"], self.synth_equalizer_settings[eql][e]["ceq3"], self.synth_equalizer_settings[eql][e]["ceq4"] )


    # Save edited equalizer parameters to an equalizer
    #   eql:: Equalizer setting number (0..EQUALIZERS-1)
    #   eq#:: Three equalizers parameter hash {"ceq0".."ceq4"}
    def save_edited_data_to_equalizer( self, eql, eq0, eq1, eq2 ):
        if eql >= 0 and eql < self.EQUALIZERS:
            for c in range(5):
                self.synth_equalizer_settings[eql][0]["ceq"+str(c)] = eq0["ceq"+str(c)]

            for c in range(5):
                self.synth_equalizer_settings[eql][1]["ceq"+str(c)] = eq1["ceq"+str(c)]

            for c in range(5):
                self.synth_equalizer_settings[eql][2]["ceq"+str(c)] = eq2["ceq"+str(c)]


    # Get equalizer parameters
    #   eql:: Equalizer setting number (0..EQUALIZERS-1)
    #   RETURN:: Equalizer three parameters [0..2]{"ceq0".."ceq4"}
    def get_equalizer_parameters( self, eql ):
        if eql >= 0 and eql < self.EQUALIZERS:
            return( self.synth_equalizer_settings[eql] )

        return( None )


    # Set sample sound parameters to YMF825.
    #   GLOBAL sound_param[0]:: byte for register address (to be set it later)
    #   GLOBAL sound_param[1..35]:: tone data
#    def set_preset_tone2( self, timbre_from=0, timbre_to=self.TIMBRE_PORTIONS-1 ):
    def set_preset_tone2( self ):
        #HED: 0,0x81,
        ##Address
        self.sound_param[ 0]=0
        ##Header 0x80 + voices(=16)
        self.sound_param[ 1]=0x80 + self.VOICES
    
        #BLS: 0x01,0x85,
        ##Basic octave
        self.sound_param[ 2]=1
        ##LFO*64 + Algorithm
        self.sound_param[ 3]=2*64+6
    
        #OP1: 0x00,0x7F,0xF4,0xBB,0x00,0x10,0x40,
        ##OP1:Sustin rate*16 + Ignore key off*8 + Key scale sensitivity
        self.sound_param[ 4]=0*16+0*8+0
        ##OP1:Release rate*16 + Decay rate
#    self.sound_param[ 5]=7*16+15
        self.sound_param[ 5]=15*16+15
        ##OP1:Atack rate*16 + Sustin level
        self.sound_param[ 6]=15*16+4
        ##OP1:Total operator level*16 + Key scaling level sensitivity
        self.sound_param[ 7]=11*16+11
        ##OP1:Depth of amp modulation*32 + Enable amp mod*16 + Depth of vibrato*2 + Enable vivlato
        self.sound_param[ 8]=0*32+0*16+0*2+0
        ##OP1:Multi contol magnification frequency*16 + Detune
        self.sound_param[ 9]=1*16+0
        ##OP1:Wave shape*8 + FM feedback level
#    self.sound_param[10]=7*64+0
        self.sound_param[10]=7*8+0
    
        #OP2: 0x00,0xAF,0xA0,0x0E,0x03,0x10,0x40,
        ##OP2:Sustin rate*16 + Ignore key off*8 + Key scale sensitivity
        self.sound_param[11]=0*16+0*8+0
        ##OP2:Release rate*16 + Decay rate
        self.sound_param[12]=10*16+15
        ##OP2:Atack rate*16 + Sustin level
        self.sound_param[13]=10*16+0
        ##OP2:Total operator level*16 + Key scaling level sensitivity
        self.sound_param[14]=0*16+14
        ##OP2:Depth of amp modulation*32 + Enable amp mod*16 + Depth of vibrato*2 + Enable vivlato
        self.sound_param[15]=0*32+0*16+0*2+3
        ##OP2:Multi contol magnification frequency*16 + Detune
        self.sound_param[16]=1*16+0
        ##OP2:Wave shape*8 + FM feedback level
#    self.sound_param[17]=7*64+0
        self.sound_param[17]=7*8+0
    
        #OP3: 0x00,0x2F,0xF3,0x9B,0x00,0x20,0x41,
        ##OP3:Sustin rate*16 + Ignore key off*8 + Key scale sensitivity
        self.sound_param[18]=0*16+0*8+0
        ##OP3:Release rate*16 + Decay rate
#   self.sound_param[19]=2*16+15
        self.sound_param[19]=15*16+15
        ##OP3:Atack rate*16 + Sustin level
        self.sound_param[20]=15*16+3
        ##OP3:Total operator level*16 + Key scaling level sensitivity
        self.sound_param[21]=9*16+11
        ##OP3:Depth of amp modulation*32 + Enable amp mod*16 + Depth of vibrato*2 + Enable vivlato
        self.sound_param[22]=0*32+0*16+0*2+0
        ##OP3:Multi contol magnification frequency*16 + Detune
        self.sound_param[23]=2*16+0
        ##OP3:Wave shape*8 + FM feedback level
#    self.sound_param[24]=7*64+1
        self.sound_param[24]=7*8+1
    
        #OP4: 0x00,0xAF,0xA0,0x0E,0x01,0x10,0x40,
        ##OP4:Sustin rate*16 + Ignore key off*8 + Key scale sensitivity
        self.sound_param[25]=0*16+0*8+0
        ##OP4:Release rate*16 + Decay rate
        self.sound_param[26]=10*16+15
        ##OP4:Atack rate*16 + Sustin level
        self.sound_param[27]=10*16+0
        ##OP4:Total operator level*16 + Key scaling level sensitivity
        self.sound_param[28]=0*16+14
        ##OP4:Depth of amp modulation*32 + Enable amp mod*16 + Depth of vibrato*2 + Enable vivlato
        self.sound_param[29]=0*32+0*16+0*2+1
        ##OP4:Multi contol magnification frequency*16 + Detune
        self.sound_param[30]=1*16+0
        ##OP4:Wave shape*8 + FM feedback level
#    self.sound_param[31]=7*64+0
        self.sound_param[31]=7*8+0
    
        # TRAILER CODES: 0x80,0x03,0x81,0x80
        self.sound_param[32]=0x80
        self.sound_param[33]=0x03
        self.sound_param[34]=0x81
        self.sound_param[35]=0x80
    
        self.synth_tones[2] = self.sound_param.copy()
        self.synth_tone_names[2] = "PRESET TONE2"


    # Set default sound parameters to YMF825.
    # Must be called to set header and trailer byte into timbre sound data list.
    def set_preset_tone01( self, tone ):
    #    sound_param = [0,0x80 + VOICES] + ([0x01,0x85,0x00,0x7F,0xF4,0xBB,0x00,0x10,0x40,0x00,0xAF,0xA0,0x0E,0x03,0x10,0x40,0x00,0x2F,0xF3,0x9B,0x00,0x20,0x41,0x00,0xAF,0xA0,0x0E,0x01,0x10,0x40]*VOICES) + [0x80,0x03,0x81,0x80]
        self.sound_param = [0,0x80 + self.VOICES] + [0x01,0x85,0x00,0x7F,0xF4,0xBB,0x00,0x10,0x40,0x00,0xAF,0xA0,0x0E,0x03,0x10,0x40,0x00,0x2F,0xF3,0x9B,0x00,0x20,0x41,0x00,0xAF,0xA0,0x0E,0x01,0x10,0x40] + [0x80,0x03,0x81,0x80]
        self.synth_tones[tone] = self.sound_param.copy()
        if tone == 0:
            self.synth_tone_names[tone] = "EDITING"
        else:
            self.synth_tone_names[tone] = "PRESET TONE" + str(tone)


    # Load tone data.
    def load_tone_data( self ):
        try:
            file = open( self.tone_name_file, encoding = self.file_encode )
        except OSError as e:
            print(e)
        else:
            self.synth_tone_names = json.load( file )
            file.close()

        try:
            file = open( self.tone_param_file , encoding = self.file_encode )
        except OSError as e:
            print(e)
        else:
            self.synth_tones = json.load( file )
            file.close()


    # Load timbre data.
    def load_timbre_data( self ):
        try:
            file = open( self.timbre_name_file, encoding = self.file_encode )
        except OSError as e:
            print(e)
        else:
            self.synth_timbre_names = json.load( file )
            file.close()

        try:
            file = open( self.timbre_param_file, encoding = self.file_encode )
        except OSError as e:
            print(e)
        else:
            self.synth_timbres = json.load( file )
            file.close()


    # Load equalizer data.
    def load_equalizer_data( self ):
        try:
            file = open( self.equalizer_name_file, encoding = self.file_encode )
        except OSError as e:
            print(e)
        else:
            self.synth_equalizer_names = json.load( file )
            file.close()

        try:
            file = open( self.equalizer_param_file , encoding = self.file_encode )
        except OSError as e:
            print(e)
        else:
            self.synth_equalizer_settings = json.load( file )
            file.close()


    # Save tone data.
    def save_tone_data( self, name_file = "YMF825ToneName.txt", tone_file = "YMF825ToneParm.txt", encode = "utf-8" ):
        try:
            file = open( name_file, "w", encoding = encode )
        except OSError as e:
            print(e)
        else:
#            json.dump( self.synth_tone_names, file, indent = 4 )
            json.dump( self.synth_tone_names, file )
            file.close()

        try:
            file = open( tone_file, "w", encoding = encode )
        except OSError as e:
            print(e)
        else:
#            json.dump( self.synth_tones, file, indent = 4 )
            json.dump( self.synth_tones, file )
            file.close()


    # Save timbre data.
    def save_timbre_data( self, name_file = "YMF825TimbreName.txt", timbre_file = "YMF825TimbreParm.txt", encode = "utf-8" ):
        try:
            file = open( name_file, "w", encoding = encode )
        except OSError as e:
            print(e)
        else:
#            json.dump( self.synth_timbre_names, file, indent = 4 )
            json.dump( self.synth_timbre_names, file )
            file.close()

        try:
            file = open( timbre_file, "w", encoding = encode )
        except OSError as e:
            print(e)
        else:
#            json.dump( self.synth_timbres, file, indent = 4 )
            json.dump( self.synth_timbres, file )
            file.close()


    # Save equalizer data.
    def save_equalizer_data( self, name_file = "YMF825EQName.txt", equalizer_file = "YMF825EQParm.txxt", encode = "utf-8" ):
        try:
            file = open( name_file, "w", encoding = encode )
        except OSError as e:
            print(e)
        else:
#            json.dump( self.synth_equalizer_names, file, indent = 4 )
            json.dump( self.synth_equalizer_names, file )
            file.close()

        try:
            file = open( equalizer_file, "w", encoding = encode )
        except OSError as e:
            print(e)
        else:
#            json.dump( self.synth_equalizer_settings, file, indent = 4 )
            json.dump( self.synth_equalizer_settings, file )
            file.close()


    # Reset and Initialize YMF825.
    def init_YMF825( self ):
        self.YMF825_reset.high()
        print("RESET HIGH")
        self.delay(1000)
        self.YMF825_reset.low()
        print("RESET LOW")
        self.delay(1000)
        self.YMF825_reset.high()
        self.delay(1000)
        print("Reset YMF825.")
      
        self.spi_write_byte( 0x1D, 0x00 )
        self.spi_write_byte( 0x02, 0x0E )
        self.delay(20)
      
        self.spi_write_byte( 0x00, 0x01 )
        self.spi_write_byte( 0x01, 0x00 )
        self.spi_write_byte( 0x1A, 0xA3 )
        self.delay(20)
      
        self.spi_write_byte( 0x1A, 0x00 )
        self.delay( 40 )
      
        self.spi_write_byte( 0x02, 0x04 )
        self.delay( 20 )
    
        self.spi_write_byte( 0x02, 0x00 )
    
        # add
        self.spi_write_byte( 0x19, 0xFF )
        self.spi_write_byte( 0x1B, 0x3F )
        self.spi_write_byte( 0x14, 0x00 )
        self.spi_write_byte( 0x03, 0x01 )
    
        self.spi_write_byte( 0x08, 0xF6 )
        self.delay( 40 )
        self.spi_write_byte( 0x08, 0x00 )
        self.spi_write_byte( 0x09, 0xF8 )
        self.spi_write_byte( 0x0A, 0x00 )
    
        self.spi_write_byte( 0x17, 0x40 )
        self.spi_write_byte( 0x18, 0x00 )
    
        print("YMF825 initialized.")


    # Set up hardware.
    def setup_hardware( self ):
        print("SPI uses CE0(pin24/port8)")
        self.led_turn( True )
        self.chip_select( False )

        print("spi object=", self.spi)
        print("Set up YMF825")
        self.init_YMF825()


    # Set up software
    def setup_synth( self ):
        # Clear tone data
        for t in range(1,self.TONES):
            self.synth_tones[t] = [0,0x80 + self.VOICES]+[0]*30+[0x80,0x03,0x81,0x80]

        # Clear timbre data
        for t in range(1,self.TIMBRES):
            self.synth_timbres[t] = [
                                        {"voice_from":  0, "voice_to":  7, "tone": 1},
                                        {"voice_from":  8, "voice_to": 11, "tone": 2},
                                        {"voice_from": 12, "voice_to": 13, "tone": 1},
                                        {"voice_from": 14, "voice_to": 15, "tone": 2}
                                    ]

        #Initialize EDITING tone (to be overwritten by load_tone_data)
        self.set_preset_tone01( 0 )

        # Load tone data
        self.load_tone_data()

        # load timbre data
        self.load_timbre_data()

        # load equalizer data
        self.load_equalizer_data()

        # Preset tones 1 and 2 (not to be overwritten by load_tone_data)
        self.set_preset_tone01( 1 )
        self.set_preset_tone2()

        # Timbre0 is EDITING timbre (not to be overwritten by load_timbre_data)
        self.synth_timbre_names[0] = "EDITING"
        self.synth_timbres[0][0]["voice_from"] = 0
        self.synth_timbres[0][0]["voice_to"]   = self.VOICES-1
        self.synth_timbres[0][1]["voice_from"] = -1
        self.synth_timbres[0][1]["voice_to"]   = -1
        self.synth_timbres[0][2]["voice_from"] = -1
        self.synth_timbres[0][2]["voice_to"]   = -1
        self.synth_timbres[0][3]["voice_from"] = -1
        self.synth_timbres[0][3]["voice_to"]   = -1
        self.set_timbre_portion_tone( 0, 0, 0 )
        self.set_timbre_portion_tone( 0, 1, 0 )
        self.set_timbre_portion_tone( 0, 2, 0 )
        self.set_timbre_portion_tone( 0, 3, 0 )

#        self.set_playing_timbre( self.synth_play_timbre )
        self.set_synth_play_timbre( self.synth_play_timbre )
        self.set_timbre_tones( self.synth_play_timbre )
        self.set_chanel()

        # Equalizer1 must be path-through filter
        self.synth_equalizer_names[0] = "EDITING"
        self.synth_equalizer_names[1] = "ALL PATH"
        print("EQ PARAMS:", self.synth_equalizer_settings[1])
        for eq in range(3):
            self.synth_equalizer_settings[1][eq]["ceq0"] = 1.0
            self.synth_equalizer_settings[1][eq]["ceq1"] = 0.0
            self.synth_equalizer_settings[1][eq]["ceq2"] = 0.0
            self.synth_equalizer_settings[1][eq]["ceq3"] = 0.0
            self.synth_equalizer_settings[1][eq]["ceq4"] = 0.0

        self.set_synth_equalizer(0)

        print("Finished setting up.")
        self.led_turn(False)


    # Initialize application.
    def init( self ):
        print("Initialize Application.")
#        GPIO.setmode( GPIO.BCM )


    # Turn the Synthsize on
    def turn_on_synthesizer( self ):
        self.init()
        self.setup_hardware()


    # Play demo
    def play_demo( self ):
        print("YMF825pico Opeing Melody.")
        self.set_synth_play_timbre( 1 )
        self.set_timbre_tones( 1 )

        self.play_by_timbre_scale(0,"C4")
        self.delay(500)
        self.stop_by_timbre_scale(0,"C4")
        self.delay(500)
        self.play_by_timbre_scale(0,"E4")
        self.delay(500)
        self.stop_by_timbre_scale(0,"E4")
        self.delay(500)
        self.play_by_timbre_scale(0,"G4")
        self.delay(500)
        self.stop_by_timbre_scale(0,"G4")
        self.delay(500)
        self.play_by_timbre_scale(0,"C5")
        self.delay(500)
        self.stop_by_timbre_scale(0,"C5")
        self.delay(1000)

// code stored in the sketch: ymf825pico_synth_main.py.ino
#############################################################################
# YMF825 synthesizer with Raspberry Pi PICO W.
#
# Hardware Information:
#   YMF825 bottom view
#     1 2 3 4 5 6 7 8 9
#    -+-+-+-+-+-+-+-+-+-
#   | S M M C G V R     |
#   | S O I L N C S     |
#   |   S S K D C T     |
#   |   I O             |
#   |             Audio Jack
#    ---------------+---
#                   |
#                    ---Amp
#
#   PICO GPIO(pin)      YMF825 name(pin)    LED(n/a)
#     5V          (40)    VCC        (6)
#     GND         (38)    GND        (5)
#     SPI1 MOSI 19(25)    SPI MOSI   (2)
#     SPI1 MISO 16(21)    SPI MISO   (3)
#     SPI1 CLK  18(24)    SPI CLK    (4)
#     SPI1 CS   17(22)    SS         (1)
#     RESET     22(29)    RESET      (7)
#n/a  LED       28(34)                      Anode---1K--->|---Cathode---GND
#
#   PICO GPIO(pin)      SSD1306 name(pin)    LED(n/a)
#     I2C0 SDA  20(24)    SDA        (4)
#     I2C0 SCL  21(25)    SCL        (3)
#                         GND        (2)
#                         VCC(3.3V)  (1)
#
# Copyright (c) by Shunsuke Ohira
#   00.100 2023/08/05: Play Do-Re-Mi
#############################################################################

from ymf825pico import ymf825pico_class
from machine import Pin, I2C, SPI, UART
import ssd1306
import time
import gc

# UART test
UART_CH = 0
UART_TX = 0   # GPIO No.
UART_RX = 1   # GPIO No.
#UART_BAUDRATE = 9600
UART_BAUDRATE = 31250

# I2C for SSD1306 OLED Display
I2C_SSD1306_CH = 0
I2C_SSD1306_SDA = 20    # Pin24
I2C_SSD1306_SCL = 21    # Pin25

# SSD1306 OLED Display
DISPLAY_WIDTH = 128
DISPLAY_HEIGHT = 64
DISPLAT_HALF_WIDTH = int(DISPLAY_WIDTH / 2)
DISPLAY_DIVIDE = 83
DISPLAY_LINE_HEIGHT = 10
DISPLAY_MENU_LINES= 4
display = None

# I2C for SSD1306 OLED Display
i2c_ssd1306 = I2C(I2C_SSD1306_CH, sda=Pin(I2C_SSD1306_SDA), scl=Pin(I2C_SSD1306_SCL))

# Rotary encoders
ROTARY_ENCODERS = [
    # No.     GPIO No.                Pin objects                 Previous pin values       Pjn values             Pin No.
    {"NO": 0, "A_PIN": 2, "B_PIN": 3, "A_SW": None, "B_SW": None, "A_PREV": 2, "B_PREV": 2, "VALUES": [0,0,0,0]},  # Pin 4,  5
    {"NO": 1, "A_PIN": 4, "B_PIN": 5, "A_SW": None, "B_SW": None, "A_PREV": 2, "B_PREV": 2, "VALUES": [0,0,0,0]},  # Pin 6,  7
    {"NO": 2, "A_PIN": 6, "B_PIN": 7, "A_SW": None, "B_SW": None, "A_PREV": 2, "B_PREV": 2, "VALUES": [0,0,0,0]},  # Pin 9, 10
    {"NO": 3, "A_PIN": 8, "B_PIN": 9, "A_SW": None, "B_SW": None, "A_PREV": 2, "B_PREV": 2, "VALUES": [0,0,0,0]}   # Pin11, 12
]

# YMF825 parameters mapping and order (ABBR, REAL KEY NAME, VALUE RANGE)
PARM_TEXT_OFF_ON = ["OFF", "ON"]
PARM_TEXT_ALGO = ["Ab", "A+b", "AbCd+", "A+bc", "Abcd", "Ab+Cd", "A+bcd", "A+bc+d"]
PARM_TEXT_WAVE = [
    "SIN",   "SIN/2", "SINSN", "SAILs",
    "SIN*2", "S*2/2", "SQUAR", "RIBBN",
    "SINcp", "Scp/2", "ScpSc", "SAILc",
    "Scp*2", "Sc2/2", "SQR/2", "-----",
    "TRIAN", "TRI/2", "TRITR", "SAILt",
    "TRI*2", "TR2/2", "SQR*2", "-----",
    "RAMP",  "RMP/2", "RMPRP", "SAILr",
    "RMP*2", "RRM/2", "SQ2/2", "-----"
]
YMF825_PARM = [
    # GENERAL
    ("Basic OCT", "Basic Octave", 4, None),
    ("Algorithm", "Algorithm", 8, PARM_TEXT_ALGO),
    ("LFO", "LFO", 8, None),
    # OP1
    ("Wave Shp A", "Wave Shape1", 32, PARM_TEXT_WAVE),
    ("Total LV A", "Total Operator Level1", 64, None),
    ("Feedback A", "FM Feedback Level1", 8, None),
    ("Detune   A", "Detune1", 8, None),
    ("MCM Freq A", "Multi Control Magnification Frequency1", 16, None),
    ("Atack RT A", "Attack Rate1", 16, None),
    ("Decay RT A", "Decay Rate1", 16, None),
    ("Sustn LV A", "Sustain Level1", 16, None),
    ("Sustn RT A", "Sustain Rate1", 16, None),
    ("Reles RT A", "Release Rate1", 16, None),
    ("Vibrt EN A", "Enable Vibrate1", 2, PARM_TEXT_OFF_ON),
    ("Vibrt DP A", "Depth Of Vibrate1", 4, None),
    ("Amp M EN A", "Enable Amp Modulation1", 2, PARM_TEXT_OFF_ON),
    ("Amp M DP A", "Depth Of Amp Modulation1", 4, None),
    ("Key S EN A", "Key Scale Sensitivity1", 2, PARM_TEXT_OFF_ON),
    ("Key S LV A", "Key Scale Level Sensivitiy1", 4, None),
    ("IgnKy OF A", "Ignore Key Off1", 2, PARM_TEXT_OFF_ON),
    # OP2
    ("Wave Shp B", "Wave Shape2", 32, PARM_TEXT_WAVE),
    ("Total LV B", "Total Operator Level2", 64, None),
    ("Feedback B", "FM Feedback Level2", 8, None),
    ("Detune   B", "Detune2", 8, None),
    ("MCM Freq B", "Multi Control Magnification Frequency2", 16, None),
    ("Atack RT B", "Attack Rate2", 16, None),
    ("Decay RT B", "Decay Rate2", 16, None),
    ("Sustn LV B", "Sustain Level2", 16, None),
    ("Sustn RT B", "Sustain Rate2", 16, None),
    ("Reles RT B", "Release Rate2", 16, None),
    ("Vibrt EN B", "Enable Vibrate2", 2, PARM_TEXT_OFF_ON),
    ("Vibrt DP B", "Depth Of Vibrate2", 4, None),
    ("Amp M EN B", "Enable Amp Modulation2", 2, PARM_TEXT_OFF_ON),
    ("Amp M DP B", "Depth Of Amp Modulation2", 4, None),
    ("Key S EN B", "Key Scale Sensitivity2", 2, PARM_TEXT_OFF_ON),
    ("Key S LV B", "Key Scale Level Sensivitiy2", 4, None),
    ("IgnKy OF B", "Ignore Key Off2", 2, PARM_TEXT_OFF_ON),
    # OP3
    ("Wave Shp C", "Wave Shape3", 32, PARM_TEXT_WAVE),
    ("Total LV C", "Total Operator Level3", 64, None),
    ("Feedback C", "FM Feedback Level3", 8, None),
    ("Detune   C", "Detune3", 8, None),
    ("MCM Freq C", "Multi Control Magnification Frequency3", 16, None),
    ("Atack RT C", "Attack Rate3", 16, None),
    ("Decay RT C", "Decay Rate3", 16, None),
    ("Sustn LV C", "Sustain Level3", 16, None),
    ("Sustn RT C", "Sustain Rate3", 16, None),
    ("Reles RT C", "Release Rate3", 16, None),
    ("Vibrt EN C", "Enable Vibrate3", 2, PARM_TEXT_OFF_ON),
    ("Vibrt DP C", "Depth Of Vibrate3", 4, None),
    ("Amp M EN C", "Enable Amp Modulation3", 2, PARM_TEXT_OFF_ON),
    ("Amp M DP C", "Depth Of Amp Modulation3", 4, None),
    ("Key S EN C", "Key Scale Sensitivity3", 2, PARM_TEXT_OFF_ON),
    ("Key S LV C", "Key Scale Level Sensivitiy3", 4, None),
    ("IgnKy OF C", "Ignore Key Off3", 2, PARM_TEXT_OFF_ON),
    # OP4
    ("Wave Shp D", "Wave Shape4", 32, PARM_TEXT_WAVE),
    ("Total LV D", "Total Operator Level4", 64, None),
    ("Feedback D", "FM Feedback Level4", 8, None),
    ("Detune   D", "Detune4", 8, None),
    ("MCM Freq D", "Multi Control Magnification Frequency4", 16, None),
    ("Atack RT D", "Attack Rate4", 16, None),
    ("Decay RT D", "Decay Rate4", 16, None),
    ("Sustn LV D", "Sustain Level4", 16, None),
    ("Sustn RT D", "Sustain Rate4", 16, None),
    ("Reles RT D", "Release Rate4", 16, None),
    ("Vibrt EN D", "Enable Vibrate4", 2, PARM_TEXT_OFF_ON),
    ("Vibrt DP D", "Depth Of Vibrate4", 4, None),
    ("Amp M EN D", "Enable Amp Modulation4", 2, PARM_TEXT_OFF_ON),
    ("Amp M DP D", "Depth Of Amp Modulation4", 4, None),
    ("Key S EN D", "Key Scale Sensitivity4", 2, PARM_TEXT_OFF_ON),
    ("Key S LV D", "Key Scale Level Sensivitiy4", 4, None),
    ("IgnKy OF D", "Ignore Key Off4", 2, PARM_TEXT_OFF_ON),
]

# Character list
CHARS_LIST= ["="]   # No change
CHARS_LIST += [chr(ch) for ch in list(range(0x41,0x5b))]
CHARS_LIST += [chr(ch) for ch in list(range(0x30,0x3a))]
CHARS_LIST += [" "]

# YMF825pico menu
menu_main = 0
menu_category = 0
menu_item = 0
menu_value = 0

#--- YMF825pico menu definitions
# PLAY
MAIN_MENU_PLAY_MANUAL = 0
MAIN_MENU_PLAY = 0
MAIN_MENU_PLAY_DEMO = 1

# TIMBRE NAME
MAIN_MENU_TIMBRE_NAME = 1
TIMBRE_NAME_LENGTH = 10

# TIMBRE EDIT
MAIN_MENU_TIMBRE_EDIT = 2

# TONE NAME
MAIN_MENU_TONE_NAME = 3
TONE_NAME_LENGTH = 10

# TONE EDIT
MAIN_MENU_TONE_EDIT = 4

# TONE COPY
MAIN_MENU_TONE_COPY = 5


# Show menu
# move_dir: 1=down, -1=up
def show_menu(move_dir):
    global menu_main, menu_category, menu_item, menu_value

#    print(SYNTH_MENU)
#    print(menu_main, menu_category, menu_item, menu_value)

    # Show MAIN and CATEGORY
    main_name = SYNTH_MENU[menu_main]["name"]
    category_name = SYNTH_MENU[menu_main]["CATEGORY"][menu_category]["name"]
    if main_name == "TONE EDIT":
        selected = SYNTH_MENU[menu_main]["CATEGORY"][menu_category]["ITEM"][1]["selected"]
        algo = SYNTH_MENU[menu_main]["CATEGORY"][menu_category]["ITEM"][1]["VALUE"][selected]["name"]
        print("ALGO=", menu_main, menu_category, selected, algo)
        main_name = main_name + ":" + algo

    display.fill(0)
    display.text(main_name, 0, 0, True)
    display.hline(0, DISPLAY_LINE_HEIGHT - 2, DISPLAY_WIDTH, True)
    display.text(category_name, 0, DISPLAY_LINE_HEIGHT, True)
    display.hline(0, DISPLAY_LINE_HEIGHT * 2 - 2, DISPLAY_WIDTH, True)
    display.vline(DISPLAY_DIVIDE, DISPLAY_LINE_HEIGHT * 2 - 2, DISPLAY_HEIGHT - (DISPLAY_LINE_HEIGHT * 2 - 2), True)

    # Show ITEM and VALUE
    items = len(SYNTH_MENU[menu_main]["CATEGORY"][menu_category]["ITEM"])
    if menu_item < DISPLAY_MENU_LINES:
        menu_s = 0
    elif menu_item >= items - DISPLAY_MENU_LINES:
        menu_s = items - DISPLAY_MENU_LINES
    elif move_dir == 1:
        menu_s = menu_item - DISPLAY_MENU_LINES + 1
    else:
        menu_s = menu_item

#    print("MOVE DIR, s, e=", move_dir, menu_s, menu_s + DISPLAY_MENU_LINES)
    y = DISPLAY_LINE_HEIGHT * 2
    for i in list(range(menu_s, min(items, menu_s + DISPLAY_MENU_LINES))):
        # Show ITEM
        item_name = SYNTH_MENU[menu_main]["CATEGORY"][menu_category]["ITEM"][i]["name"]
        display.text(item_name, 0, y, True)
        
        # Show the current editing VALUE
        if i == menu_item:
            value_name = SYNTH_MENU[menu_main]["CATEGORY"][menu_category]["ITEM"][i]["VALUE"][menu_value]["name"]
            display.hline(0, y + DISPLAY_LINE_HEIGHT - 2, DISPLAY_WIDTH, True)
        # Show the selected VALUE
        else:
            selected = int(SYNTH_MENU[menu_main]["CATEGORY"][menu_category]["ITEM"][i]["selected"])
#            print("MENU:", menu_main, menu_category, i, selected)
            value_name = SYNTH_MENU[menu_main]["CATEGORY"][menu_category]["ITEM"][i]["VALUE"][selected]["name"]

#        print("SHOW=", value_name)
        display.text(value_name, DISPLAY_DIVIDE + 2, y, True)
        y += DISPLAY_LINE_HEIGHT

    display.show()


# Clear list memory for SYNTH_MENU
def clear_menu_memory(prev, clear_category, clear_item, clear_value):
    if prev < 0:
        return

    target_main = menu_main
    target_category = menu_category
    target_item = menu_item
    if clear_category:
        target_main = prev
    elif clear_item:
        target_category = prev
    elif clear_value:
        target_item = prev
        
    print("CLEAR:", clear_category, clear_item, clear_value)
    print("TARGET: MAIN={} CATEGORY={} ITEM={}".format(target_main, target_category, target_item))
    print("LENGTH: CATEGORY={} ITEM={} VALUE={}".format(len(SYNTH_MENU[target_main]["CATEGORY"]), len(SYNTH_MENU[target_main]["CATEGORY"][target_category]["ITEM"]), len(SYNTH_MENU[target_main]["CATEGORY"][target_category]["ITEM"][target_item]["VALUE"])))
    if clear_value:
        del SYNTH_MENU[target_main]["CATEGORY"][target_category]["ITEM"][target_item]["VALUE"]
        SYNTH_MENU[target_main]["CATEGORY"][target_category]["ITEM"][target_item]["VALUE"] = []

    if clear_item:
        del SYNTH_MENU[target_main]["CATEGORY"][target_category]["ITEM"]
        SYNTH_MENU[target_main]["CATEGORY"][target_category]["ITEM"] = []

    if clear_category:
        del SYNTH_MENU[target_main]["CATEGORY"]
        SYNTH_MENU[target_main]["CATEGORY"] = []

    gc.collect()


#--- MAIN MENE: PLAY
# Make select play menu (PLAY)
def make_select_play_menu(menu, prev_menu):
    global YMF825pico

    clear_menu_memory(prev_menu, True, True, True)

    SYNTH_MENU[MAIN_MENU_PLAY]["CATEGORY"] = [
        {   # MAIN_MENU_PLAY_MANUAL
            "name": "MANUAL",
            "on_select": make_select_timbre_menu,
            "on_selected": None,
            "ITEM": []
        },
        {   # MAIN_MENU_PLAY_DEMO
            "name": "DEMO",
            "on_select": make_select_demo_menu,
            "on_selected": None,
            "ITEM": []
        }
    ]
    
    if SYNTH_MENU[menu_main]["CATEGORY"][menu_category]["on_select"] is not None:
        SYNTH_MENU[menu_main]["CATEGORY"][menu_category]["on_select"](0, -1)

    if SYNTH_MENU[menu_main]["CATEGORY"][menu_category]["ITEM"][menu_item]["on_select"] is not None:
        SYNTH_MENU[menu_main]["CATEGORY"][menu_category]["ITEM"][menu_item]["on_select"](0, -1)

    if SYNTH_MENU[menu_main]["CATEGORY"][menu_category]["ITEM"][menu_item]["VALUE"][menu_value]["on_select"] is not None:
        SYNTH_MENU[menu_main]["CATEGORY"][menu_category]["ITEM"][menu_item]["VALUE"][menu_value]["on_select"](0, -1)


# Make select timbre menu (PLAY>MANUAL>timbre list>selelct)
def make_select_timbre_menu(menu, prev_menu):
    global YMF825pico

    clear_menu_memory(prev_menu, False, True, True)

    tmb_list = YMF825pico.get_synth_timbre_names()
    SYNTH_MENU[MAIN_MENU_PLAY]["CATEGORY"][MAIN_MENU_PLAY_MANUAL]["ITEM"] = []
    for tmb in tmb_list:
        SYNTH_MENU[MAIN_MENU_PLAY]["CATEGORY"][MAIN_MENU_PLAY_MANUAL]["ITEM"].append({"name": tmb, "on_select": None, "on_selected": None, "selected": 0, "VALUE": [{"name": "NO", "on_select": None, "on_selected": None}, {"name": "SET", "on_select": on_select_timbre, "on_selected": None}]})


#--- MAIN MENE: DEMO
# Make select demo menu (PLAY>MANUAL>demo list>selelct)
def make_select_demo_menu(menu, prev_menu):
    clear_menu_memory(prev_menu, False, True, True)

    demo_list = ["DEMO1", "DEMO2", "DEMO3"]
    SYNTH_MENU[MAIN_MENU_PLAY]["CATEGORY"][MAIN_MENU_PLAY_DEMO]["ITEM"] = []
    for demo in demo_list:
        SYNTH_MENU[MAIN_MENU_PLAY]["CATEGORY"][MAIN_MENU_PLAY_DEMO]["ITEM"].append({"name": demo, "on_select": None, "on_selected": None, "selected": 0, "VALUE": [{"name": "NO", "on_select": None, "on_selected": None}, {"name": "PLAY", "on_select": None, "on_selected": on_play_demo}]})


# Select a timbre on the menu
def on_select_timbre():
    global YMF825pico

    # Set new timbre to YMF825pico class, then send a change timbre command to YMF825
    print("CHANGE TIMBRE TO ", SYNTH_MENU[menu_main]["CATEGORY"][menu_category]["ITEM"][menu_item]["name"])
    YMF825pico.set_synth_play_timbre(menu_item)
    YMF825pico.set_timbre_tones(menu_item)


# Play a demo score
def on_play_demo(demo = None):
    global YMF825pico

    # Play a demo
    if demo is None:
        demo = SYNTH_MENU[menu_main]["CATEGORY"][menu_category]["ITEM"][menu_item]["name"]

    print("PLAY DEMO=", demo)
    if demo == "DEMO1":
        YMF825pico.play_by_timbre_scale(0,"C4")
        YMF825pico.delay(500)
        YMF825pico.stop_by_timbre_scale(0,"C4")
        
        YMF825pico.play_by_timbre_scale(0,"E4")
        YMF825pico.delay(500)
        YMF825pico.stop_by_timbre_scale(0,"E4")
        
        YMF825pico.play_by_timbre_scale(0,"G4")
        YMF825pico.delay(500)
        YMF825pico.stop_by_timbre_scale(0,"G4")

        YMF825pico.play_by_timbre_scale(0,"C5")
        YMF825pico.delay(500)
        YMF825pico.stop_by_timbre_scale(0,"C5")

    elif demo == "DEMO2":
        YMF825pico.play_by_timbre_scale(0,"C4")
        YMF825pico.delay(500)
        YMF825pico.play_by_timbre_scale(0,"E4")
        YMF825pico.delay(500)
        YMF825pico.play_by_timbre_scale(0,"G4")
        YMF825pico.delay(500)
        YMF825pico.play_by_timbre_scale(0,"C5")
        YMF825pico.delay(500)
        YMF825pico.stop_by_timbre_scale(0,"C4")
        YMF825pico.stop_by_timbre_scale(0,"E4")
        YMF825pico.stop_by_timbre_scale(0,"G4")
        YMF825pico.stop_by_timbre_scale(0,"C5")

    elif demo == "DEMO3":
        YMF825pico.play_by_timbre_scale(0,"C4")
        YMF825pico.play_by_timbre_scale(1,"C4")
        YMF825pico.delay(500)
        YMF825pico.stop_by_timbre_scale(0,"C4")
        YMF825pico.stop_by_timbre_scale(1,"C4")
        
        YMF825pico.play_by_timbre_scale(0,"E4")
        YMF825pico.play_by_timbre_scale(1,"E4")
        YMF825pico.delay(500)
        YMF825pico.stop_by_timbre_scale(0,"E4")
        YMF825pico.stop_by_timbre_scale(1,"E4")

        YMF825pico.play_by_timbre_scale(0,"G4")
        YMF825pico.play_by_timbre_scale(1,"G4")
        YMF825pico.delay(500)
        YMF825pico.stop_by_timbre_scale(0,"G4")
        YMF825pico.stop_by_timbre_scale(1,"G4")

        YMF825pico.play_by_timbre_scale(0,"C5")
        YMF825pico.play_by_timbre_scale(1,"C5")
        YMF825pico.delay(500)
        YMF825pico.stop_by_timbre_scale(0,"C5")
        YMF825pico.stop_by_timbre_scale(1,"C5")


#--- MAIN MENE: TIMBRE NAME
# Make edit timbre name menu (TIMBRE>timbre list>timbre name>selelct)
def make_edit_timbre_name_menu(menu, prev_menu):
    global YMF825pico

    clear_menu_memory(prev_menu, True, True, True)

    timbre_list = YMF825pico.get_synth_timbre_names()
    SYNTH_MENU[MAIN_MENU_TIMBRE_NAME]["CATEGORY"] = []
    for timbre in timbre_list:
        values = []
        for ch in CHARS_LIST:
            values.append({"name": ch, "on_select": on_change_char, "on_selected": None})

        # Current timbre name as ITEM menu
        item = []
        for i in list(range(TIMBRE_NAME_LENGTH)):
            ch = timbre[i:i+1]
            if ch == "":
                ch = " "
            item.append({"name": ch, "on_select": None, "on_selected": None, "selected": 0, "VALUE": values})

        item.append({"name": "SAVE",   "on_select": None, "on_selected": None, "selected": 0, "VALUE": [{"name": "NO", "on_select": None, "on_selected": None}, {"name": "SURE?", "on_select": None, "on_selected": None}, {"name": "YES", "on_select": on_save_timbre_name, "on_selected": None}]})
        item.append({"name": "CANCEL", "on_select": None, "on_selected": None, "selected": 0, "VALUE": [{"name": "NO", "on_select": None, "on_selected": None}, {"name": "SURE?", "on_select": None, "on_selected": None}, {"name": "YES", "on_select": on_cancel_timbre_name, "on_selected": None}]})

        SYNTH_MENU[MAIN_MENU_TIMBRE_NAME]["CATEGORY"].append({"name": timbre, "on_select": None, "on_selected": None, "ITEM": item})


# Cancel the changes to timbre name
def on_cancel_timbre_name():
    global menu_main, menu_category, menu_item, menu_value

    # Clear selected data and initialize the TIMBRE NAME menu
    menu_item = 0
    for itm in SYNTH_MENU[menu_main]["CATEGORY"][menu_category]["ITEM"]:
        itm["selected"] = 0

    menu_value = SYNTH_MENU[menu_main]["CATEGORY"][menu_category]["ITEM"][menu_item]["selected"]
    show_menu(1)


# Change a timbre name and save all timbre data
def on_save_timbre_name():
    global YMF825pico
    global menu_main, menu_category, menu_item, menu_value

    # Change the current tone name
    name = ""
    for i in list(range(TIMBRE_NAME_LENGTH)):
        ch = CHARS_LIST[SYNTH_MENU[menu_main]["CATEGORY"][menu_category]["ITEM"][i]["selected"]]
        name += ch if ch != CHARS_LIST[0] else SYNTH_MENU[menu_main]["CATEGORY"][menu_category]["ITEM"][i]["name"]

    print("CHANGE TIMBRE NAME[{}]={}".format(menu_category, name))
    YMF825pico.rename_timbre(menu_category, name)

    # Save tone data
    YMF825pico.save_timbre_data()

    # Initialize the TONE NAME menu
    make_edit_timbre_name_menu(menu_main, menu_main)
    on_cancel_timbre_name()


#--- MAIN MENE: TIMBRE EDIT
# Make timbre edit menu
def make_edit_timbre_edit_menu(menu, prev_menu):
    global YMF825pico

    clear_menu_memory(prev_menu, True, True, True)

    tone_list = YMF825pico.get_synth_tone_names()
    values_tone = []
    for tone in tone_list:
        values_tone.append({"name": tone, "on_select": on_change_timbre_edit, "on_selected": None})

    values_voice = []
    for voice in list(range(16)):
        values_voice.append({"name": str(voice), "on_select": on_change_timbre_edit, "on_selected": None})

    values_volume = []
    for volume in list(range(32)):
        values_volume.append({"name": str(volume), "on_select": on_change_timbre_edit, "on_selected": None})

    timbre_list = YMF825pico.get_synth_timbre_names()
    print("TIMBER LIST:", timbre_list)
    SYNTH_MENU[MAIN_MENU_TIMBRE_EDIT]["CATEGORY"] = []
    timbre_id = 0
    for timbre in timbre_list:

        # TIMBER SET ITEM menu
        item = []
        for portion in list(range(YMF825pico.TIMBRE_PORTIONS)):
            item.append({"name": "TONE{}".format(portion), "on_select": None, "on_selected": None, "selected": YMF825pico.get_timbre_tone(timbre_id, portion), "VALUE": values_tone})
            item.append({"name": "VOICE L{}".format(portion), "on_select": None, "on_selected": None, "selected": YMF825pico.get_timbre_voice_from(timbre_id, portion), "VALUE": values_voice})
            item.append({"name": "VOICE H{}".format(portion), "on_select": None, "on_selected": None, "selected": YMF825pico.get_timbre_voice_to(timbre_id, portion), "VALUE": values_voice})
            item.append({"name": "VOLUME{}".format(portion), "on_select": None, "on_selected": None, "selected": YMF825pico.get_timbre_volume(timbre_id, portion), "VALUE": values_volume})

        item.append({"name": "SAVE",   "on_select": None, "on_selected": None, "selected": 0, "VALUE": [{"name": "NO", "on_select": None, "on_selected": None}, {"name": "SURE?", "on_select": None, "on_selected": None}, {"name": "YES", "on_select": on_save_timbre_edit, "on_selected": None}]})
        item.append({"name": "CANCEL", "on_select": None, "on_selected": None, "selected": 0, "VALUE": [{"name": "NO", "on_select": None, "on_selected": None}, {"name": "SURE?", "on_select": None, "on_selected": None}, {"name": "YES", "on_select": on_cancel_timbre_edit, "on_selected": None}]})

        SYNTH_MENU[MAIN_MENU_TIMBRE_EDIT]["CATEGORY"].append({"name": timbre, "on_select": None, "on_selected": None, "ITEM": item})
        timbre_id += 1


def on_change_timbre_edit():
    global menu_main, menu_category, menu_item, menu_value
    SYNTH_MENU[menu_main]["CATEGORY"][menu_category]["ITEM"][menu_item]["selected"] = menu_value


def on_cancel_timbre_edit():
    global menu_main, menu_category, menu_item, menu_value

    # Clear selected data and initialize the TIMBRE NAME menu
    menu_item = 0
    make_edit_timbre_edit_menu(menu_main, menu_main)
    menu_value = SYNTH_MENU[menu_main]["CATEGORY"][menu_category]["ITEM"][menu_item]["selected"]
    show_menu(1)


def on_save_timbre_edit():
    global YMF825pico
    global menu_main, menu_category, menu_item, menu_value

    # Change the current timbre settings
    print("CHANGE TIMBRE SETTINGS[{}]".format(menu_category))
    for portion in list(range(YMF825pico.TIMBRE_PORTIONS)):
        i = portion * 4
        tone = SYNTH_MENU[menu_main]["CATEGORY"][menu_category]["ITEM"][i]["selected"]
        YMF825pico.set_timbre_portion_tone(menu_category, portion, tone)

        vfrom = SYNTH_MENU[menu_main]["CATEGORY"][menu_category]["ITEM"][i+1]["selected"]
        vto   = SYNTH_MENU[menu_main]["CATEGORY"][menu_category]["ITEM"][i+2]["selected"]
        YMF825pico.set_timbre_voice_range(menu_category, portion, vfrom, vto)

        volume = SYNTH_MENU[menu_main]["CATEGORY"][menu_category]["ITEM"][i+3]["selected"]
        YMF825pico.set_timbre_portion_volume(menu_category, portion, volume)

    # Save timbre data
    YMF825pico.save_timbre_data()
    on_cancel_timbre_edit()


#--- MAIN MENE: TONE NAME
# Make edit tone name menu (TONE>tone list>tone name>selelct)
def make_edit_tone_name_menu(menu, prev_menu):
    global YMF825pico

    clear_menu_memory(prev_menu, True, True, True)

    tone_list = YMF825pico.get_synth_tone_names()
    SYNTH_MENU[MAIN_MENU_TONE_NAME]["CATEGORY"] = []
    for tone in tone_list:
        values = []
        for ch in CHARS_LIST:
            values.append({"name": ch, "on_select": on_change_char, "on_selected": None})

        # Current tone name as ITEM menu
        item = []
        for i in list(range(TONE_NAME_LENGTH)):
            ch = tone[i:i+1]
            if ch == "":
                ch = " "
            item.append({"name": ch, "on_select": None, "on_selected": None, "selected": 0, "VALUE": values})

        item.append({"name": "SAVE",   "on_select": None, "on_selected": None, "selected": 0, "VALUE": [{"name": "NO", "on_select": None, "on_selected": None}, {"name": "SURE?", "on_select": None, "on_selected": None}, {"name": "YES", "on_select": on_save_tone_name, "on_selected": None}]})
        item.append({"name": "CANCEL", "on_select": None, "on_selected": None, "selected": 0, "VALUE": [{"name": "NO", "on_select": None, "on_selected": None}, {"name": "SURE?", "on_select": None, "on_selected": None}, {"name": "YES", "on_select": on_cancel_tone_name, "on_selected": None}]})

        SYNTH_MENU[MAIN_MENU_TONE_NAME]["CATEGORY"].append({"name": tone, "on_select": None, "on_selected": None, "ITEM": item})


# Change a character data
def on_change_char():
    global menu_main, menu_category, menu_item, menu_value
    SYNTH_MENU[menu_main]["CATEGORY"][menu_category]["ITEM"][menu_item]["selected"] = menu_value


# Cancel the changes to tone name
def on_cancel_tone_name():
    global menu_main, menu_category, menu_item, menu_value

    # Clear selected data and initialize the TONE NAME menu
    menu_item = 0
    for itm in SYNTH_MENU[menu_main]["CATEGORY"][menu_category]["ITEM"]:
        itm["selected"] = 0

    menu_value = SYNTH_MENU[menu_main]["CATEGORY"][menu_category]["ITEM"][menu_item]["selected"]
    show_menu(1)


# Change a tone name and save all tone data
def on_save_tone_name():
    global YMF825pico
    global menu_main, menu_category, menu_item, menu_value

    # Change the current tone name
    name = ""
    for i in list(range(TONE_NAME_LENGTH)):
        ch = CHARS_LIST[SYNTH_MENU[menu_main]["CATEGORY"][menu_category]["ITEM"][i]["selected"]]
        name += ch if ch != CHARS_LIST[0] else SYNTH_MENU[menu_main]["CATEGORY"][menu_category]["ITEM"][i]["name"]

    print("CHANGE TONE NAME[{}]={}".format(menu_category, name))
    YMF825pico.rename_tone(menu_category, name)

    # Save tone data
    YMF825pico.save_tone_data()

    # Initialize the TONE NAME menu
    make_edit_tone_name_menu(menu_main, menu_main)
    on_cancel_tone_name()


#--- MAIN MENE: TONE EDIT
# Make edit tone edit menu (TONE EDIT>tone list>parameter name>selelct)
def make_edit_tone_edit_menu(menu, prev_menu):
    global YMF825pico

    clear_menu_memory(prev_menu, True, True, True)

    tone_list = YMF825pico.get_synth_tone_names()
    SYNTH_MENU[MAIN_MENU_TONE_EDIT]["CATEGORY"] = []
#    tone_id = 0
    for tone in tone_list:
        item = []

        item.append({"name": "SAVE",   "on_select": None, "on_selected": None, "selected": 0, "VALUE": [{"name": "NO", "on_select": None, "on_selected": None}, {"name": "SURE?", "on_select": None, "on_selected": None}, {"name": "YES", "on_select": on_save_tone_edit, "on_selected": None}]})
        item.append({"name": "CANCEL", "on_select": None, "on_selected": None, "selected": 0, "VALUE": [{"name": "NO", "on_select": None, "on_selected": None}, {"name": "SURE?", "on_select": None, "on_selected": None}, {"name": "YES", "on_select": on_cancel_tone_edit, "on_selected": None}]})

        SYNTH_MENU[MAIN_MENU_TONE_EDIT]["CATEGORY"].append({"name": tone, "on_select": on_select_tone_edit_tone, "on_selected": None, "ITEM": item})
#        tone_id += 1


# Make tone editor menu
def on_select_tone_edit_tone(menu, prev_menu):
    global YMF825pico

    # Remake ITEM>VALUE menu
    print("MENU={} CLEAR PREV={}".format(menu, prev_menu))
    clear_menu_memory(prev_menu, False, True, True)

    # Get tone data for editing
    tone_hash = YMF825pico.copy_tone_data_for_edit(menu_category)
    print("TONE HASH[{}]:".format(menu_category))

    values_parm = []
    for num in list(range(64)):
        values_parm.append({"name": str(num), "on_select": on_change_tone_parm, "on_selected": None})
        
    item = []
    for parm_def in YMF825_PARM:
        parm = parm_def[0]        
        print("PARM[{}/{}] = {}".format(parm, parm_def[1], tone_hash[parm_def[1]]))
        if parm_def[3] is None:
            item.append({"name": parm, "on_select": on_select_tone_parm, "on_selected": None, "selected": tone_hash[parm_def[1]], "VALUE": values_parm[0:parm_def[2]]})
        else:
            item.append({"name": parm, "on_select": on_select_tone_parm, "on_selected": None, "selected": tone_hash[parm_def[1]], "VALUE": [{"name": nm, "on_select": on_change_tone_parm, "on_selected": None} for nm in parm_def[3]]})

    item.append({"name": "SAVE",   "on_select": None, "on_selected": None, "selected": 0, "VALUE": [{"name": "NO", "on_select": None, "on_selected": None}, {"name": "SURE?", "on_select": None, "on_selected": None}, {"name": "YES", "on_select": on_save_tone_edit, "on_selected": None}]})
    item.append({"name": "CANCEL", "on_select": None, "on_selected": None, "selected": 0, "VALUE": [{"name": "NO", "on_select": None, "on_selected": None}, {"name": "SURE?", "on_select": None, "on_selected": None}, {"name": "YES", "on_select": on_cancel_tone_edit, "on_selected": None}]})
    SYNTH_MENU[MAIN_MENU_TONE_EDIT]["CATEGORY"][menu_category]["ITEM"] = item

    # Set EDITING Timbre
    YMF825pico.save_edited_data_to_tone(0)
    YMF825pico.set_synth_play_timbre(0)
    YMF825pico.set_timbre_tones(0)


def on_select_tone_parm(menu, prev_menu):
    if reflect_tone_edit():
        on_play_demo("DEMO1")


def on_change_tone_parm():
    global menu_main, menu_category, menu_item, menu_value

    SYNTH_MENU[menu_main]["CATEGORY"][menu_category]["ITEM"][menu_item]["selected"] = menu_value


def on_cancel_tone_edit():
    global menu_main, menu_category, menu_item, menu_value

    # Clear selected data and initialize the TONE NAME menu
    menu_item = 0
    on_select_tone_edit_tone(menu_category, menu_category)
    menu_value = SYNTH_MENU[menu_main]["CATEGORY"][menu_category]["ITEM"][menu_item]["selected"]
    show_menu(1)


prev_parm_hash = {}
def reflect_tone_edit():
    global YMF825pico
    global menu_main, menu_category, menu_item, menu_value, prev_parm_hash

    # Make edited tone parameters' hash
    parm_hash = {}
    for parm_def in YMF825_PARM:
        abbr = parm_def[0]
        pkey = parm_def[1]
        for item in SYNTH_MENU[menu_main]["CATEGORY"][menu_category]["ITEM"]:
            if item["name"] == abbr:
                parm_hash[pkey] = item["selected"]

    # Save tone parameters' data
    if parm_hash != prev_parm_hash:
        for parm in parm_hash.keys():
            print("PARM[{}] = {}".format(parm, parm_hash[parm]))

        YMF825pico.set_editing_tone(parm_hash)
        YMF825pico.save_edited_data_to_tone(0)
        YMF825pico.set_synth_play_timbre(0)
        YMF825pico.set_timbre_tones(0)
        prev_parm_hash = parm_hash.copy()
        return True
    else:
        print("PARM NOT CHANGED.")
        return False


def on_save_tone_edit():
    if reflect_tone_edit():
        YMF825pico.save_edited_data_to_tone(menu_category)
        YMF825pico.save_tone_data()

    on_play_demo("DEMO1")
    on_cancel_tone_edit()


#--- MAIN MENU: TONE COPY
# Make edit tone copy menu (TONE COPY>tone list>tone list>selelct)
def make_edit_tone_copy_menu(menu, prev_menu):
    global YMF825pico

    clear_menu_memory(prev_menu, True, True, True)

    tone_list = YMF825pico.get_synth_tone_names()
    SYNTH_MENU[MAIN_MENU_TONE_COPY]["CATEGORY"] = []
    for tone in tone_list:
        item = []

        item.append({"name": "SAVE",   "on_select": None, "on_selected": None, "selected": 0, "VALUE": [{"name": "NO", "on_select": None, "on_selected": None}, {"name": "SURE?", "on_select": None, "on_selected": None}, {"name": "YES", "on_select": on_save_tone_edit, "on_selected": None}]})
        item.append({"name": "CANCEL", "on_select": None, "on_selected": None, "selected": 0, "VALUE": [{"name": "NO", "on_select": None, "on_selected": None}, {"name": "SURE?", "on_select": None, "on_selected": None}, {"name": "YES", "on_select": on_cancel_tone_edit, "on_selected": None}]})

        SYNTH_MENU[MAIN_MENU_TONE_COPY]["CATEGORY"].append({"name": tone, "on_select": on_select_tone_copy_tone, "on_selected": None, "ITEM": item})


# Make copy target tone list as the item list
def on_select_tone_copy_tone(menu, prev_menu):
    global YMF825pico

    clear_menu_memory(prev_menu, False, True, True)

    item = []
    values_parm = [
        {"name": "NO", "on_select": None, "on_selected": None},
        {"name": "SURE?", "on_select": None, "on_selected": None},
        {"name": "YES", "on_select": on_change_copy_parm, "on_selected": None}
    ]
    tone_list = YMF825pico.get_synth_tone_names()
    for tone in tone_list:
        item.append({"name": tone, "on_select": None, "on_selected": None, "selected": 0, "VALUE": values_parm})

    item.append({"name": "SAVE",   "on_select": None, "on_selected": None, "selected": 0, "VALUE": [{"name": "NO", "on_select": None, "on_selected": None}, {"name": "SURE?", "on_select": None, "on_selected": None}, {"name": "YES", "on_select": on_save_tone_edit, "on_selected": None}]})
    item.append({"name": "CANCEL", "on_select": None, "on_selected": None, "selected": 0, "VALUE": [{"name": "NO", "on_select": None, "on_selected": None}, {"name": "SURE?", "on_select": None, "on_selected": None}, {"name": "YES", "on_select": on_cancel_tone_edit, "on_selected": None}]})
    SYNTH_MENU[MAIN_MENU_TONE_COPY]["CATEGORY"][menu_category]["ITEM"] = item


# Copy a tone to another one
def on_change_copy_parm():
    global YMF825pico
    global menu_main, menu_category, menu_item, menu_value, prev_parm_hash

    print("Copy tone {} to {}.".format(menu_category, menu_item))
    if menu_category != menu_item:
        # Get tone data for editing
        tone_hash = YMF825pico.copy_tone_data_for_edit(menu_category)
        print("TONE HASH[{}]:".format(menu_category))
        YMF825pico.set_editing_tone(tone_hash)
        YMF825pico.save_edited_data_to_tone(menu_item)


# YMF825pico 4 layers' menu structures: MAIN>CATEGORY>ITEM>VALUE
SYNTH_MENU = [
    {   # MAIN_MENU_PLAY
        "name": "PLAY",
        "on_select": make_select_play_menu,
        "on_selected": None,
        "CATEGORY": [
            {   # MAIN_MENU_PLAY_MANUAL
                "name": "MANUAL",
                "on_select": make_select_timbre_menu,
                "on_selected": None,
                "ITEM": []
            },
            {   # MAIN_MENU_PLAY_DEMO
                "name": "DEMO",
                "on_select": make_select_demo_menu,
                "on_selected": None,
                "ITEM": []
            }
        ]
    },
    {   # MAIN_MENU_TIMBRE_NAME
        "name": "TIMBRE NAME",
        "on_select": make_edit_timbre_name_menu,
        "on_selected": None,
        "CATEGORY": []
    },
    {   # MAIN_MENU_TIMBRE_EDIT
        "name": "TIMBRE EDIT",
        "on_select": make_edit_timbre_edit_menu,
        "on_selected": None,
        "CATEGORY": []
    },
    {   # MAIN_MENU_TONE_NAME
        "name": "TONE NAME",
        "on_select": make_edit_tone_name_menu,
        "on_selected": None,
        "CATEGORY": []
    },
    {   # MAIN_MENU_TONE_EDIT
        "name": "TONE EDIT",
        "on_select": make_edit_tone_edit_menu,
        "on_selected": None,
        "CATEGORY": []
    },
    {   # MAIN_MENU_TONE_COPY
        "name": "TONE COPY",
        "on_select": make_edit_tone_copy_menu,
        "on_selected": None,
        "CATEGORY": []
    }
]


# Get a rotary encoder status
# rte: {"NO": ?, "A_PIN": gpio, "B_PIN": gpio, "A_SW": pin object, "B_SW": pin object, "A_PREV": ?, "B_PREV": ?, "VALUES": [0,0,0,0]}
# RETURN:
#   1=count up
#  -1=count down
#   0=stay
def get_a_rotary_encoder(rte):
    a = rte["A_SW"].value()
    b = rte["B_SW"].value()
    time.sleep(0.001)
    if rte["A_PREV"] != a or rte["B_PREV"] != b:
        del rte["VALUES"][0]
        rte["VALUES"].append(rte["A_PREV"] * 8 + rte["B_PREV"] * 4 + a * 2 + b)
        rte["A_PREV"] = a
        rte["B_PREV"] = b
#        print("A, B=", a, b)
#        print("BUF[{}]={},{},{},{}".format(rte["NO"], bin(rte["VALUES"][0]), bin(rte["VALUES"][1]), bin(rte["VALUES"][2]), bin(rte["VALUES"][3])))

        if rte["VALUES"] == [0b1101, 0b0100, 0b0010, 0b1011]:
            return 1
        
        if rte["VALUES"] == [0b1110, 0b1000, 0b0001, 0b0111]:
            return -1

    return 0


# Get rotary encoders' status
def get_rotary_encoders():
    global menu_main, menu_category, menu_item, menu_value

    # Rotary encoder pins
    for rte in ROTARY_ENCODERS:
        count = get_a_rotary_encoder(rte)
        if count != 0:
#            print("ROTARY ENCODER[{}] = {}".format(rte["NO"], count))
            
            # MAIN
            if rte["NO"] == 0:
                menu_main += count
                if menu_main < 0:
#                    menu_main = 0
                    menu_main = len(SYNTH_MENU) - 1
                elif menu_main >= len(SYNTH_MENU):
#                    menu_main = len(SYNTH_MENU) - 1
                    menu_main = 0
                else:
                    if SYNTH_MENU[menu_main]["on_select"] is not None:
                        SYNTH_MENU[menu_main]["on_select"](menu_main, menu_main - count)
                        
                    # Change menu
                    menu_category = 0
                    menu_item = 0
                    print("MENU: MAIN={} CATEGORY={} ITEM={}".format(menu_main, menu_category, menu_item))
                    print("LENG: MAIN={}".format(len(SYNTH_MENU)))
                    print("LENG: CATEGORY={}".format(len(SYNTH_MENU[menu_main]["CATEGORY"])))
                    print("LENG: ITEM={}".format(len(SYNTH_MENU[menu_main]["CATEGORY"][menu_category]["ITEM"])))
                    print("ITEM: SELECTED={}".format(SYNTH_MENU[menu_main]["CATEGORY"][menu_category]["ITEM"][menu_item]["selected"]))
                    menu_value = SYNTH_MENU[menu_main]["CATEGORY"][menu_category]["ITEM"][menu_item]["selected"]
                    show_menu(count)

                    if SYNTH_MENU[menu_main]["on_selected"] is not None:
                        SYNTH_MENU[menu_main]["on_selected"](menu_main, menu_main - count)

            # CATEGORY
            elif rte["NO"] == 1:
                menu_category += count
                if menu_category < 0:
#                    menu_category = 0
                    menu_category = len(SYNTH_MENU[menu_main]["CATEGORY"]) - 1
                elif menu_category >= len(SYNTH_MENU[menu_main]["CATEGORY"]):
#                    menu_category = len(SYNTH_MENU[menu_main]["CATEGORY"]) - 1
                    menu_category = 0
                else:
                    if SYNTH_MENU[menu_main]["CATEGORY"][menu_category]["on_select"] is not None:
                        SYNTH_MENU[menu_main]["CATEGORY"][menu_category]["on_select"](menu_category, menu_category - count)

                    # Change menu
                    menu_item = 0
                    menu_value = SYNTH_MENU[menu_main]["CATEGORY"][menu_category]["ITEM"][menu_item]["selected"]
                    show_menu(count)

                    if SYNTH_MENU[menu_main]["CATEGORY"][menu_category]["on_selected"] is not None:
                        SYNTH_MENU[menu_main]["CATEGORY"][menu_category]["on_selected"](menu_category,menu_category - count)

            # ITEM
            elif rte["NO"] == 2:
                menu_item += count
                if menu_item < 0:
#                    menu_item = 0
                    menu_item = len(SYNTH_MENU[menu_main]["CATEGORY"][menu_category]["ITEM"]) - 1
                elif menu_item >= len(SYNTH_MENU[menu_main]["CATEGORY"][menu_category]["ITEM"]):
#                    menu_item = len(SYNTH_MENU[menu_main]["CATEGORY"][menu_category]["ITEM"]) - 1
                    menu_item = 0
                else:
                    if SYNTH_MENU[menu_main]["CATEGORY"][menu_category]["ITEM"][menu_item]["on_select"] is not None:
                        SYNTH_MENU[menu_main]["CATEGORY"][menu_category]["ITEM"][menu_item]["on_select"](menu_item, menu_item - count)

                    # Change menu
                    menu_value = SYNTH_MENU[menu_main]["CATEGORY"][menu_category]["ITEM"][menu_item]["selected"]
                    show_menu(count)

                    if SYNTH_MENU[menu_main]["CATEGORY"][menu_category]["ITEM"][menu_item]["on_selected"] is not None:
                        SYNTH_MENU[menu_main]["CATEGORY"][menu_category]["ITEM"][menu_item]["on_selected"](menu_item, menu_item - count)

            # VALUE
            elif rte["NO"] == 3:
                menu_value += count
                if menu_value < 0:
                    menu_value = 0
                elif menu_value >= len(SYNTH_MENU[menu_main]["CATEGORY"][menu_category]["ITEM"][menu_item]["VALUE"]):
                    menu_value = len(SYNTH_MENU[menu_main]["CATEGORY"][menu_category]["ITEM"][menu_item]["VALUE"]) - 1
                else:
                    if SYNTH_MENU[menu_main]["CATEGORY"][menu_category]["ITEM"][menu_item]["VALUE"][menu_value]["on_select"] is not None:
                        SYNTH_MENU[menu_main]["CATEGORY"][menu_category]["ITEM"][menu_item]["VALUE"][menu_value]["on_select"]()

                    # Change menu
                    show_menu(count)

                    if SYNTH_MENU[menu_main]["CATEGORY"][menu_category]["ITEM"][menu_item]["VALUE"][menu_value]["on_selected"] is not None:
                        SYNTH_MENU[menu_main]["CATEGORY"][menu_category]["ITEM"][menu_item]["VALUE"][menu_value]["on_selected"]()


#Receive MIDI (work in a thread)
def midi_interface(midi_events, length):
    timbre = 0

    bt = 0
    while bt < length:
        # MIDI command
        midi_cmd  = midi_events[bt]
        bt += 1
        left = length - bt

        # note on: 0x9n (n=0..f: MIDI CH)
        if midi_cmd == 0x90:
            if left >= 2:
                # MIDI note
                midi_note = midi_events[bt]
                # MIDI velocity
                midi_velo = midi_events[bt + 1]
                bt += 2
                YMF825pico.play_by_timbre_note(timbre, midi_note, midi_velo)

        # note off
        elif midi_cmd == 0x80:
            if left >= 2:
                # MIDI note
                midi_note = midi_events[bt]
                # MIDI velocity
                midi_velo = midi_events[bt + 1]
                bt += 2
                YMF825pico.stop_by_timbre_note(timbre, midi_note)
    
        # Control
        elif midi_cmd == 0xB0:
            if left >= 2:
                # MIDI note
                midi_note = midi_events[bt]
                # MIDI velocity
                midi_velo = midi_events[bt + 1]
                bt += 2
                
                # sustain: pressed:[2]==0x7f / released [2]==0
                if midi_note == 0x40:
                    YMF825pico.sustain_pedal(timbre, midi_velo == 0x7f)

                # modulation
                elif midi_cmd == 176 and midi_note == 1:
                    pass
    
    '''
    # pitch+ --> timbre+
    elif midi_cmd == 224 and midi_note == 71:
        timbre = ( timbre + 1 ) % 4
        updated_timbre_portion(timbre)
    
    # pitch- --> timbre-
    elif midi_cmd == 224 and midi_note == 57:
        timbre = ( timbre - 1 ) % 4
        updated_timbre_portion(timbre)
    '''


'''
# Play tones with UART
tone_kye_map = {
    "z": ["C3", False],
    "s": ["C3#", False],
    "x": ["D3", False],
    "d": ["D3#", False],
    "c": ["E3", False],
    "v": ["F3", False],
    "g": ["F3#", False],
    "b": ["G3", False],
    "h": ["G3#", False],
    "n": ["A3", False],
    "j": ["A3#", False],
    "m": ["B3", False],
    "Z": ["C4", False],
    "S": ["C4#", False],
    "X": ["D4", False],
    "D": ["D4#", False],
    "C": ["E4", False],
    "V": ["F4", False],
    "G": ["F4#", False],
    "B": ["G4", False],
    "H": ["G4#", False],
    "N": ["A4", False],
    "J": ["A4#", False],
    "M": ["B4", False]
}
tone_key_timbre = 0
def all_note_off(timbre):
    for k in tone_kye_map.keys():
        if tone_kye_map[k][1]:
            YMF825pico.stop_by_timbre_scale(timbre, tone_kye_map[k][0])
            tone_kye_map[k][1] = False


def play_tone_with_uart_keyboard(key_byte, length):
    global tone_key_timbre

    # Play tones
    if length > 0:
        for k in list(range(length)):
            c = chr(key_byte[k])
            print("KEY=", k, c)
            if c in tone_kye_map:
                tone = tone_kye_map[c][0]
                if tone_kye_map[c][1] == False:
                    YMF825pico.play_by_timbre_scale(tone_key_timbre, tone)
                    tone_kye_map[c][1] = True
            elif c == "0":
                all_note_off(tone_key_timbre)
                tone_key_timbre = 0
            elif c == "1":
                all_note_off(tone_key_timbre)
                tone_key_timbre = 1
            elif c == "2":
                all_note_off(tone_key_timbre)
                tone_key_timbre = 2
            elif c == "3":
                all_note_off(tone_key_timbre)
                tone_key_timbre = 3
    # All note off
    else:
        all_note_off(tone_key_timbre)
'''


#Set up hardware
def setup():
    print("setup.")

    # Menu initialize
    if SYNTH_MENU[menu_main]["on_select"] is not None:
        SYNTH_MENU[menu_main]["on_select"](0, -1)

    if SYNTH_MENU[menu_main]["CATEGORY"][menu_category]["on_select"] is not None:
        SYNTH_MENU[menu_main]["CATEGORY"][menu_category]["on_select"](0, -1)

    if SYNTH_MENU[menu_main]["CATEGORY"][menu_category]["ITEM"][menu_item]["on_select"] is not None:
        SYNTH_MENU[menu_main]["CATEGORY"][menu_category]["ITEM"][menu_item]["on_select"](0, -1)

    if SYNTH_MENU[menu_main]["CATEGORY"][menu_category]["ITEM"][menu_item]["VALUE"][menu_value]["on_select"] is not None:
        SYNTH_MENU[menu_main]["CATEGORY"][menu_category]["ITEM"][menu_item]["VALUE"][menu_value]["on_select"](0, -1)

    print("setup end.")


#Initialize application
def init():
    global display
    
    print("init.")

    # SSD1306 setup
    addr = i2c_ssd1306.scan()
    print("SSD1306 ADDRESS=" + hex(addr[0]))
    display = ssd1306.SSD1306_I2C(DISPLAY_WIDTH, DISPLAY_HEIGHT, i2c_ssd1306)
    print("SSD1306 display=", display)
    display.contrast(128)
    display.fill(0)
    display.text("YMF825pico", 25, 20, True)
    display.hline(0, 30, DISPLAY_WIDTH, True)
    display.text("(C)2023, S.Ohira", 0, 33, True)
    display.show()

    # Rotary encoder pins
    for rte in ROTARY_ENCODERS:
        rte["A_SW"] = Pin(rte["A_PIN"], Pin.IN, Pin.PULL_UP)
        rte["B_SW"] = Pin(rte["B_PIN"], Pin.IN, Pin.PULL_UP)

    print("init() end.")


#Main
if __name__=='__main__':
    # CPU clock 240MHz
#    machine.freq(133000000)
    machine.freq(240000000)

    # UART
    uart = UART(UART_CH, baudrate=UART_BAUDRATE, tx=Pin(UART_TX), rx=Pin(UART_RX), bits=8, parity=None, stop=1)

    # YMF825
    YMF825pico = ymf825pico_class()
    init()
    setup()

    # YMF825 control class
    print("YMF825 PICO CLASS")
    YMF825pico.turn_on_synthesizer()
    YMF825pico.setup_synth()

    YMF825pico.play_demo()

    show_menu(1)

    # UART
    recv = 0
    uart_read = True

    while True:
        # Get rotary encoders
        get_rotary_encoders()

        # MIDI keyboard UART receive
        length = uart.any()
        if length > 0:
            read_bytes = uart.read(length)
#            print("UART:[", recv, ":", length, "]=", read_bytes)
#            for bt in read_bytes:
#                print("data=", hex(bt))
            uart_read = True

            if length == 3:
                midi_interface(read_bytes, length)

        elif uart_read:
            print("UART: waiting...")
            uart_read = False

        '''
        # PC keyboard UART receive
        length = uart.any()
        if length > 0:
            recv += 1
            read_bytes = uart.read(length)
            print("UART:[", recv, ":", length, "]=", read_bytes)
            uart_read = True
            play_tone_with_uart_keyboard(read_bytes, length)
        elif uart_read:
            print("UART: waiting...")
            uart_read = False
            play_tone_with_uart_keyboard([], 0)
        '''

    print("QUIT.")
